// Logisim project ejercicios_clase_2.circ as structural Verilog: 15 circuits, main circuit NotN2T
module NotN2T (
  input  in,
  output out
);

  nand nand_1 (out, in, in);
endmodule

module AndN2T (
  input  in,
  input  in_2,
  output out
);

  wire nand_1_out;

  nand nand_1 (nand_1_out, in, in_2);
  NotN2T notn2t_1 (.in(nand_1_out), .out(out));
endmodule

module OrN2T (
  input  in,
  input  in_2,
  output out
);

  wire not_2_out, not_out;

  NotN2T \not  (.in(in), .out(not_out));
  NotN2T not_2 (.in(in_2), .out(not_2_out));
  nand nand_1 (out, not_out, not_2_out);
endmodule

module XOrN2T (
  input  In,
  input  In_2,
  output out
);

  wire andn2t_1_out, andn2t_2_out, Not_2_out, Not_out;

  NotN2T Not (.in(In), .out(Not_out));
  NotN2T Not_2 (.in(In_2), .out(Not_2_out));
  AndN2T andn2t_1 (.in(Not_out), .in_2(In_2), .out(andn2t_1_out));
  AndN2T andn2t_2 (.in(In), .in_2(Not_2_out), .out(andn2t_2_out));
  OrN2T Or (.in(andn2t_1_out), .in_2(andn2t_2_out), .out(out));
endmodule

module MuxN2T (
  input  L1,
  input  A,
  input  L0,
  output out
);

  wire andn2t_1_out, andn2t_2_out, notn2t_1_out;

  NotN2T notn2t_1 (.in(A), .out(notn2t_1_out));
  AndN2T andn2t_1 (.in(L1), .in_2(notn2t_1_out), .out(andn2t_1_out));
  AndN2T andn2t_2 (.in(A), .in_2(L0), .out(andn2t_2_out));
  OrN2T orn2t_1 (.in(andn2t_1_out), .in_2(andn2t_2_out), .out(out));
endmodule

module DMuxN2T (
  input  in,
  input  in_2,
  output out,
  output out_2
);

  wire nand_1_out, nand_2_out, nand_3_out;

  nand nand_1 (nand_1_out, in_2, in_2);
  nand nand_2 (nand_2_out, in, nand_1_out);
  nand nand_3 (nand_3_out, in_2, in);
  nand nand_4 (out, nand_2_out, nand_2_out);
  nand nand_5 (out_2, nand_3_out, nand_3_out);
endmodule

module Not16N2T (
  input  in_1,
  input  in_2,
  input  in_3,
  input  in_4,
  input  in_5,
  input  in_6,
  input  in_7,
  input  in_8,
  input  in_9,
  input  in_10,
  input  in_11,
  input  in_12,
  input  in_13,
  input  in_14,
  input  in_15,
  input  in_16,
  output out_17,
  output out_18,
  output out_19,
  output out_20,
  output out_21,
  output out_22,
  output out_23,
  output out_24,
  output out_25,
  output out_26,
  output out_27,
  output out_28,
  output out_29,
  output out_30,
  output out_31,
  output out_32
);

  NotN2T notn2t_1 (.in(in_1), .out(out_17));
  NotN2T notn2t_2 (.in(in_2), .out(out_18));
  NotN2T notn2t_3 (.in(in_3), .out(out_19));
  NotN2T notn2t_4 (.in(in_4), .out(out_20));
  NotN2T notn2t_5 (.in(in_5), .out(out_21));
  NotN2T notn2t_6 (.in(in_6), .out(out_22));
  NotN2T notn2t_7 (.in(in_7), .out(out_23));
  NotN2T notn2t_8 (.in(in_8), .out(out_24));
  NotN2T notn2t_9 (.in(in_9), .out(out_25));
  NotN2T notn2t_10 (.in(in_10), .out(out_26));
  NotN2T notn2t_11 (.in(in_11), .out(out_27));
  NotN2T notn2t_12 (.in(in_12), .out(out_28));
  NotN2T notn2t_13 (.in(in_13), .out(out_29));
  NotN2T notn2t_14 (.in(in_14), .out(out_30));
  NotN2T notn2t_15 (.in(in_15), .out(out_31));
  NotN2T notn2t_16 (.in(in_16), .out(out_32));
endmodule

module And16N2T (
  input  in_1,
  input  in_2,
  input  in_3,
  input  in_4,
  input  in_5,
  input  in_6,
  input  in_7,
  input  in_8,
  input  in_9,
  input  in_10,
  input  in_11,
  input  in_12,
  input  in_13,
  input  in_14,
  input  in_15,
  input  in_16,
  input  in_17,
  input  in_18,
  input  in_19,
  input  in_20,
  input  in_21,
  input  in_22,
  input  in_23,
  input  in_24,
  input  in_25,
  input  in_26,
  input  in_27,
  input  in_28,
  input  in_29,
  input  in_30,
  input  in_31,
  input  in_32,
  output out_33,
  output out_34,
  output out_35,
  output out_36,
  output out_37,
  output out_38,
  output out_39,
  output out_40,
  output out_41,
  output out_42,
  output out_43,
  output out_44,
  output out_45,
  output out_46,
  output out_47,
  output out_48
);

  AndN2T andn2t_1 (.in(in_1), .in_2(in_2), .out(out_33));
  AndN2T andn2t_2 (.in(in_3), .in_2(in_4), .out(out_34));
  AndN2T andn2t_3 (.in(in_5), .in_2(in_6), .out(out_35));
  AndN2T andn2t_4 (.in(in_7), .in_2(in_8), .out(out_36));
  AndN2T andn2t_5 (.in(in_9), .in_2(in_10), .out(out_37));
  AndN2T andn2t_6 (.in(in_11), .in_2(in_12), .out(out_38));
  AndN2T andn2t_7 (.in(in_13), .in_2(in_14), .out(out_39));
  AndN2T andn2t_8 (.in(in_15), .in_2(in_16), .out(out_40));
  AndN2T andn2t_9 (.in(in_17), .in_2(in_18), .out(out_41));
  AndN2T andn2t_10 (.in(in_19), .in_2(in_20), .out(out_42));
  AndN2T andn2t_11 (.in(in_21), .in_2(in_22), .out(out_43));
  AndN2T andn2t_12 (.in(in_23), .in_2(in_24), .out(out_44));
  AndN2T andn2t_13 (.in(in_25), .in_2(in_26), .out(out_45));
  AndN2T andn2t_14 (.in(in_27), .in_2(in_28), .out(out_46));
  AndN2T andn2t_15 (.in(in_29), .in_2(in_30), .out(out_47));
  AndN2T andn2t_16 (.in(in_31), .in_2(in_32), .out(out_48));
endmodule

module Or16N2T (
  input  in_1,
  input  in_2,
  input  in_3,
  input  in_4,
  input  in_5,
  input  in_6,
  input  in_7,
  input  in_8,
  input  in_9,
  input  in_10,
  input  in_11,
  input  in_12,
  input  in_13,
  input  in_14,
  input  in_15,
  input  in_16,
  input  in_17,
  input  in_18,
  input  in_19,
  input  in_20,
  input  in_21,
  input  in_22,
  input  in_23,
  input  in_24,
  input  in_25,
  input  in_26,
  input  in_27,
  input  in_28,
  input  in_29,
  input  in_30,
  input  in_31,
  input  in_32,
  output out_33,
  output out_34,
  output out_35,
  output out_36,
  output out_37,
  output out_38,
  output out_39,
  output out_40,
  output out_41,
  output out_42,
  output out_43,
  output out_44,
  output out_45,
  output out_46,
  output out_47,
  output out_48
);

  OrN2T orn2t_1 (.in(in_1), .in_2(in_2), .out(out_33));
  OrN2T orn2t_2 (.in(in_3), .in_2(in_4), .out(out_34));
  OrN2T orn2t_3 (.in(in_5), .in_2(in_6), .out(out_35));
  OrN2T orn2t_4 (.in(in_7), .in_2(in_8), .out(out_36));
  OrN2T orn2t_5 (.in(in_9), .in_2(in_10), .out(out_37));
  OrN2T orn2t_6 (.in(in_11), .in_2(in_12), .out(out_38));
  OrN2T orn2t_7 (.in(in_13), .in_2(in_14), .out(out_39));
  OrN2T orn2t_8 (.in(in_15), .in_2(in_16), .out(out_40));
  OrN2T orn2t_9 (.in(in_17), .in_2(in_18), .out(out_41));
  OrN2T orn2t_10 (.in(in_19), .in_2(in_20), .out(out_42));
  OrN2T orn2t_11 (.in(in_21), .in_2(in_22), .out(out_43));
  OrN2T orn2t_12 (.in(in_23), .in_2(in_24), .out(out_44));
  OrN2T orn2t_13 (.in(in_25), .in_2(in_26), .out(out_45));
  OrN2T orn2t_14 (.in(in_27), .in_2(in_28), .out(out_46));
  OrN2T orn2t_15 (.in(in_29), .in_2(in_30), .out(out_47));
  OrN2T orn2t_16 (.in(in_31), .in_2(in_32), .out(out_48));
endmodule

module Mux16N2T (
  input  a0,
  input  b0,
  input  a1,
  input  b1,
  input  a2,
  input  b2,
  input  a3,
  input  b3,
  input  a4,
  input  b4,
  input  a5,
  input  b5,
  input  a6,
  input  b6,
  input  a7,
  input  sel,
  input  b7,
  input  a8,
  input  b8,
  input  a9,
  input  b9,
  input  a10,
  input  b10,
  input  a11,
  input  b11,
  input  a12,
  input  b12,
  input  a13,
  input  b13,
  input  a14,
  input  b14,
  input  a15,
  input  b15,
  output out,
  output out_2,
  output out_3,
  output out_4,
  output out_5,
  output out_6,
  output out_7,
  output out_8,
  output out_9,
  output out_10,
  output out_11,
  output out_12,
  output out_13,
  output out_14,
  output out_15,
  output out_16
);

  MuxN2T muxn2t_1 (.L1(a0), .A(sel), .L0(b0), .out(out));
  MuxN2T muxn2t_2 (.L1(a1), .A(sel), .L0(b1), .out(out_2));
  MuxN2T muxn2t_3 (.L1(a2), .A(sel), .L0(b2), .out(out_3));
  MuxN2T muxn2t_4 (.L1(a3), .A(sel), .L0(b3), .out(out_4));
  MuxN2T muxn2t_5 (.L1(a4), .A(sel), .L0(b4), .out(out_5));
  MuxN2T muxn2t_6 (.L1(a5), .A(sel), .L0(b5), .out(out_6));
  MuxN2T muxn2t_7 (.L1(a6), .A(sel), .L0(b6), .out(out_7));
  MuxN2T muxn2t_8 (.L1(a7), .A(sel), .L0(b7), .out(out_8));
  MuxN2T muxn2t_9 (.L1(a8), .A(sel), .L0(b8), .out(out_9));
  MuxN2T muxn2t_10 (.L1(a9), .A(sel), .L0(b9), .out(out_10));
  MuxN2T muxn2t_11 (.L1(a10), .A(sel), .L0(b10), .out(out_11));
  MuxN2T muxn2t_12 (.L1(a11), .A(sel), .L0(b11), .out(out_12));
  MuxN2T muxn2t_13 (.L1(a12), .A(sel), .L0(b12), .out(out_13));
  MuxN2T muxn2t_14 (.L1(a13), .A(sel), .L0(b13), .out(out_14));
  MuxN2T muxn2t_15 (.L1(a14), .A(sel), .L0(b14), .out(out_15));
  MuxN2T muxn2t_16 (.L1(a15), .A(sel), .L0(b15), .out(out_16));
endmodule

module Or8Way2N2T (
  input  in_1,
  input  in_2,
  input  in_3,
  input  in_4,
  input  in_5,
  input  in_6,
  input  in_7,
  input  in_8,
  output out_9
);

  wire orn2t_1_out, orn2t_2_out, orn2t_3_out, orn2t_4_out, orn2t_5_out, orn2t_6_out;

  OrN2T orn2t_1 (.in(in_1), .in_2(in_2), .out(orn2t_1_out));
  OrN2T orn2t_2 (.in(orn2t_1_out), .in_2(in_3), .out(orn2t_2_out));
  OrN2T orn2t_3 (.in(orn2t_2_out), .in_2(in_4), .out(orn2t_3_out));
  OrN2T orn2t_4 (.in(orn2t_3_out), .in_2(in_5), .out(orn2t_4_out));
  OrN2T orn2t_5 (.in(orn2t_4_out), .in_2(in_6), .out(orn2t_5_out));
  OrN2T orn2t_6 (.in(orn2t_5_out), .in_2(in_7), .out(orn2t_6_out));
  OrN2T orn2t_7 (.in(orn2t_6_out), .in_2(in_8), .out(out_9));
endmodule

module Mux4Way16N2T (
  input  a,
  input  b,
  input  a_2,
  input  b_2,
  input  a_3,
  input  b_3,
  input  a_4,
  input  b_4,
  input  a_5,
  input  b_5,
  input  a_6,
  input  b_6,
  input  a_7,
  input  b_7,
  input  a_8,
  input  b_8,
  input  a_9,
  input  b_9,
  input  a_10,
  input  b_10,
  input  a_11,
  input  in_22,
  input  b_11,
  input  a_12,
  input  b_12,
  input  a_13,
  input  b_13,
  input  a_14,
  input  b_14,
  input  in_30,
  input  a_15,
  input  b_15,
  input  a_16,
  input  b_16,
  input  a_17,
  input  b_17,
  input  a_18,
  input  b_18,
  input  a_19,
  input  b_19,
  input  a_20,
  input  b_20,
  input  a_21,
  input  b_21,
  input  a_22,
  input  b_22,
  input  a_23,
  input  b_23,
  input  a_24,
  input  b_24,
  input  a_25,
  input  b_25,
  input  a_26,
  input  b_26,
  input  a_27,
  input  b_27,
  input  a_28,
  input  b_28,
  input  a_29,
  input  b_29,
  input  a_30,
  input  b_30,
  input  a_31,
  input  b_31,
  input  a_32,
  input  b_32,
  output out_67,
  output out_68,
  output out_69,
  output out_70,
  output out_71,
  output out_72,
  output out_73,
  output out_74,
  output out_75,
  output out_76,
  output out_77,
  output out_78,
  output out_79,
  output out_80,
  output out_81,
  output out_82
);

  wire mux16n2t_1_out, mux16n2t_1_out_2, mux16n2t_1_out_3, mux16n2t_1_out_4, mux16n2t_1_out_5,
       mux16n2t_1_out_6, mux16n2t_1_out_7, mux16n2t_1_out_8, mux16n2t_1_out_9, mux16n2t_1_out_10,
       mux16n2t_1_out_11, mux16n2t_1_out_12, mux16n2t_1_out_13, mux16n2t_1_out_14, mux16n2t_1_out_15,
       mux16n2t_1_out_16, mux16n2t_2_out, mux16n2t_2_out_2, mux16n2t_2_out_3, mux16n2t_2_out_4,
       mux16n2t_2_out_5, mux16n2t_2_out_6, mux16n2t_2_out_7, mux16n2t_2_out_8, mux16n2t_2_out_9,
       mux16n2t_2_out_10, mux16n2t_2_out_11, mux16n2t_2_out_12, mux16n2t_2_out_13, mux16n2t_2_out_14,
       mux16n2t_2_out_15, mux16n2t_2_out_16;

  Mux16N2T mux16n2t_1 (
    .a0(a), .b0(b), .a1(a_2), .b1(b_2), .a2(a_3), .b2(b_3), .a3(a_4), .b3(b_4), .a4(a_5), .b4(b_5), .a5(a_6),
    .b5(b_6), .a6(a_7), .b6(b_7), .a7(a_8), .sel(in_30), .b7(b_8), .a8(a_9), .b8(b_9), .a9(a_10), .b9(b_10),
    .a10(a_11), .b10(b_11), .a11(a_12), .b11(b_12), .a12(a_13), .b12(b_13), .a13(a_14), .b13(b_14),
    .a14(a_15), .b14(b_15), .a15(a_16), .b15(b_16), .out(mux16n2t_1_out), .out_2(mux16n2t_1_out_2),
    .out_3(mux16n2t_1_out_3), .out_4(mux16n2t_1_out_4), .out_5(mux16n2t_1_out_5), .out_6(mux16n2t_1_out_6),
    .out_7(mux16n2t_1_out_7), .out_8(mux16n2t_1_out_8), .out_9(mux16n2t_1_out_9), .out_10(mux16n2t_1_out_10),
    .out_11(mux16n2t_1_out_11), .out_12(mux16n2t_1_out_12), .out_13(mux16n2t_1_out_13),
    .out_14(mux16n2t_1_out_14), .out_15(mux16n2t_1_out_15), .out_16(mux16n2t_1_out_16));
  Mux16N2T mux16n2t_2 (
    .a0(a_17), .b0(b_17), .a1(a_18), .b1(b_18), .a2(a_19), .b2(b_19), .a3(a_20), .b3(b_20), .a4(a_21),
    .b4(b_21), .a5(a_22), .b5(b_22), .a6(a_23), .b6(b_23), .a7(a_24), .sel(in_30), .b7(b_24), .a8(a_25),
    .b8(b_25), .a9(a_26), .b9(b_26), .a10(a_27), .b10(b_27), .a11(a_28), .b11(b_28), .a12(a_29), .b12(b_29),
    .a13(a_30), .b13(b_30), .a14(a_31), .b14(b_31), .a15(a_32), .b15(b_32), .out(mux16n2t_2_out),
    .out_2(mux16n2t_2_out_2), .out_3(mux16n2t_2_out_3), .out_4(mux16n2t_2_out_4), .out_5(mux16n2t_2_out_5),
    .out_6(mux16n2t_2_out_6), .out_7(mux16n2t_2_out_7), .out_8(mux16n2t_2_out_8), .out_9(mux16n2t_2_out_9),
    .out_10(mux16n2t_2_out_10), .out_11(mux16n2t_2_out_11), .out_12(mux16n2t_2_out_12),
    .out_13(mux16n2t_2_out_13), .out_14(mux16n2t_2_out_14), .out_15(mux16n2t_2_out_15),
    .out_16(mux16n2t_2_out_16));
  Mux16N2T mux16n2t_3 (
    .a0(mux16n2t_1_out), .b0(mux16n2t_2_out), .a1(mux16n2t_1_out_2), .b1(mux16n2t_2_out_2),
    .a2(mux16n2t_1_out_3), .b2(mux16n2t_2_out_3), .a3(mux16n2t_1_out_4), .b3(mux16n2t_2_out_4),
    .a4(mux16n2t_1_out_5), .b4(mux16n2t_2_out_5), .a5(mux16n2t_1_out_6), .b5(mux16n2t_2_out_6),
    .a6(mux16n2t_1_out_7), .b6(mux16n2t_2_out_7), .a7(mux16n2t_1_out_8), .sel(in_22), .b7(mux16n2t_2_out_8),
    .a8(mux16n2t_1_out_9), .b8(mux16n2t_2_out_9), .a9(mux16n2t_1_out_10), .b9(mux16n2t_2_out_10),
    .a10(mux16n2t_1_out_11), .b10(mux16n2t_2_out_11), .a11(mux16n2t_1_out_12), .b11(mux16n2t_2_out_12),
    .a12(mux16n2t_1_out_13), .b12(mux16n2t_2_out_13), .a13(mux16n2t_1_out_14), .b13(mux16n2t_2_out_14),
    .a14(mux16n2t_1_out_15), .b14(mux16n2t_2_out_15), .a15(mux16n2t_1_out_16), .b15(mux16n2t_2_out_16),
    .out(out_67), .out_2(out_68), .out_3(out_69), .out_4(out_70), .out_5(out_71), .out_6(out_72),
    .out_7(out_73), .out_8(out_74), .out_9(out_75), .out_10(out_76), .out_11(out_77), .out_12(out_78),
    .out_13(out_79), .out_14(out_80), .out_15(out_81), .out_16(out_82));
endmodule

module Mux8Way16N2T (
  input  a,
  input  b,
  input  a_2,
  input  b_2,
  input  a_3,
  input  b_3,
  input  a_4,
  input  b_4,
  input  a_5,
  input  b_5,
  input  a_6,
  input  b_6,
  input  a_7,
  input  b_7,
  input  a_8,
  input  b_8,
  input  a_9,
  input  b_9,
  input  a_10,
  input  b_10,
  input  a_11,
  input  b_11,
  input  a_12,
  input  b_12,
  input  a_13,
  input  b_13,
  input  a_14,
  input  b_14,
  input  sel0,
  input  a_15,
  input  b_15,
  input  a_16,
  input  b_16,
  input  a_17,
  input  b_17,
  input  sel2,
  input  a_18,
  input  b_18,
  input  a_19,
  input  b_19,
  input  a_20,
  input  b_20,
  input  a_21,
  input  b_21,
  input  a_22,
  input  b_22,
  input  a_23,
  input  b_23,
  input  a_24,
  input  b_24,
  input  a_25,
  input  b_25,
  input  a_26,
  input  b_26,
  input  a_27,
  input  b_27,
  input  a_28,
  input  b_28,
  input  a_29,
  input  sel1,
  input  b_29,
  input  a_30,
  input  b_30,
  input  a_31,
  input  b_31,
  input  a_32,
  input  b_32,
  input  a_33,
  input  b_33,
  input  a_34,
  input  b_34,
  input  a_35,
  input  b_35,
  input  a_36,
  input  b_36,
  input  a_37,
  input  b_37,
  input  a_38,
  input  b_38,
  input  a_39,
  input  b_39,
  input  a_40,
  input  b_40,
  input  a_41,
  input  b_41,
  input  a_42,
  input  b_42,
  input  a_43,
  input  b_43,
  input  a_44,
  input  b_44,
  input  a_45,
  input  b_45,
  input  a_46,
  input  b_46,
  input  a_47,
  input  b_47,
  input  a_48,
  input  b_48,
  input  a_49,
  input  b_49,
  input  a_50,
  input  b_50,
  input  a_51,
  input  b_51,
  input  a_52,
  input  b_52,
  input  a_53,
  input  b_53,
  input  a_54,
  input  b_54,
  input  a_55,
  input  b_55,
  input  a_56,
  input  b_56,
  input  a_57,
  input  b_57,
  input  a_58,
  input  b_58,
  input  a_59,
  input  b_59,
  input  a_60,
  input  b_60,
  input  a_61,
  input  b_61,
  input  a_62,
  input  b_62,
  input  a_63,
  input  b_63,
  input  a_64,
  input  b_64,
  output out_132,
  output out_133,
  output out_134,
  output out_135,
  output out_136,
  output out_137,
  output out_138,
  output out_139,
  output out_140,
  output out_141,
  output out_142,
  output out_143,
  output out_144,
  output out_145,
  output out_146,
  output out_147
);

  wire mux16n2t_1_out, mux16n2t_1_out_2, mux16n2t_1_out_3, mux16n2t_1_out_4, mux16n2t_1_out_5,
       mux16n2t_1_out_6, mux16n2t_1_out_7, mux16n2t_1_out_8, mux16n2t_1_out_9, mux16n2t_1_out_10,
       mux16n2t_1_out_11, mux16n2t_1_out_12, mux16n2t_1_out_13, mux16n2t_1_out_14, mux16n2t_1_out_15,
       mux16n2t_1_out_16, mux16n2t_2_out, mux16n2t_2_out_2, mux16n2t_2_out_3, mux16n2t_2_out_4,
       mux16n2t_2_out_5, mux16n2t_2_out_6, mux16n2t_2_out_7, mux16n2t_2_out_8, mux16n2t_2_out_9,
       mux16n2t_2_out_10, mux16n2t_2_out_11, mux16n2t_2_out_12, mux16n2t_2_out_13, mux16n2t_2_out_14,
       mux16n2t_2_out_15, mux16n2t_2_out_16, mux16n2t_3_out, mux16n2t_3_out_2, mux16n2t_3_out_3,
       mux16n2t_3_out_4, mux16n2t_3_out_5, mux16n2t_3_out_6, mux16n2t_3_out_7, mux16n2t_3_out_8,
       mux16n2t_3_out_9, mux16n2t_3_out_10, mux16n2t_3_out_11, mux16n2t_3_out_12, mux16n2t_3_out_13,
       mux16n2t_3_out_14, mux16n2t_3_out_15, mux16n2t_3_out_16, mux16n2t_4_out, mux16n2t_4_out_2,
       mux16n2t_4_out_3, mux16n2t_4_out_4, mux16n2t_4_out_5, mux16n2t_4_out_6, mux16n2t_4_out_7,
       mux16n2t_4_out_8, mux16n2t_4_out_9, mux16n2t_4_out_10, mux16n2t_4_out_11, mux16n2t_4_out_12,
       mux16n2t_4_out_13, mux16n2t_4_out_14, mux16n2t_4_out_15, mux16n2t_4_out_16, mux16n2t_5_out,
       mux16n2t_5_out_2, mux16n2t_5_out_3, mux16n2t_5_out_4, mux16n2t_5_out_5, mux16n2t_5_out_6,
       mux16n2t_5_out_7, mux16n2t_5_out_8, mux16n2t_5_out_9, mux16n2t_5_out_10, mux16n2t_5_out_11,
       mux16n2t_5_out_12, mux16n2t_5_out_13, mux16n2t_5_out_14, mux16n2t_5_out_15, mux16n2t_5_out_16,
       mux16n2t_6_out, mux16n2t_6_out_2, mux16n2t_6_out_3, mux16n2t_6_out_4, mux16n2t_6_out_5,
       mux16n2t_6_out_6, mux16n2t_6_out_7, mux16n2t_6_out_8, mux16n2t_6_out_9, mux16n2t_6_out_10,
       mux16n2t_6_out_11, mux16n2t_6_out_12, mux16n2t_6_out_13, mux16n2t_6_out_14, mux16n2t_6_out_15,
       mux16n2t_6_out_16;

  Mux16N2T mux16n2t_1 (
    .a0(a), .b0(b), .a1(a_2), .b1(b_2), .a2(a_3), .b2(b_3), .a3(a_4), .b3(b_4), .a4(a_5), .b4(b_5), .a5(a_6),
    .b5(b_6), .a6(a_7), .b6(b_7), .a7(a_8), .sel(sel0), .b7(b_8), .a8(a_9), .b8(b_9), .a9(a_10), .b9(b_10),
    .a10(a_11), .b10(b_11), .a11(a_12), .b11(b_12), .a12(a_13), .b12(b_13), .a13(a_14), .b13(b_14),
    .a14(a_15), .b14(b_15), .a15(a_16), .b15(b_16), .out(mux16n2t_1_out), .out_2(mux16n2t_1_out_2),
    .out_3(mux16n2t_1_out_3), .out_4(mux16n2t_1_out_4), .out_5(mux16n2t_1_out_5), .out_6(mux16n2t_1_out_6),
    .out_7(mux16n2t_1_out_7), .out_8(mux16n2t_1_out_8), .out_9(mux16n2t_1_out_9), .out_10(mux16n2t_1_out_10),
    .out_11(mux16n2t_1_out_11), .out_12(mux16n2t_1_out_12), .out_13(mux16n2t_1_out_13),
    .out_14(mux16n2t_1_out_14), .out_15(mux16n2t_1_out_15), .out_16(mux16n2t_1_out_16));
  Mux16N2T mux16n2t_2 (
    .a0(a_17), .b0(b_17), .a1(a_18), .b1(b_18), .a2(a_19), .b2(b_19), .a3(a_20), .b3(b_20), .a4(a_21),
    .b4(b_21), .a5(a_22), .b5(b_22), .a6(a_23), .b6(b_23), .a7(a_24), .sel(sel0), .b7(b_24), .a8(a_25),
    .b8(b_25), .a9(a_26), .b9(b_26), .a10(a_27), .b10(b_27), .a11(a_28), .b11(b_28), .a12(a_29), .b12(b_29),
    .a13(a_30), .b13(b_30), .a14(a_31), .b14(b_31), .a15(a_32), .b15(b_32), .out(mux16n2t_2_out),
    .out_2(mux16n2t_2_out_2), .out_3(mux16n2t_2_out_3), .out_4(mux16n2t_2_out_4), .out_5(mux16n2t_2_out_5),
    .out_6(mux16n2t_2_out_6), .out_7(mux16n2t_2_out_7), .out_8(mux16n2t_2_out_8), .out_9(mux16n2t_2_out_9),
    .out_10(mux16n2t_2_out_10), .out_11(mux16n2t_2_out_11), .out_12(mux16n2t_2_out_12),
    .out_13(mux16n2t_2_out_13), .out_14(mux16n2t_2_out_14), .out_15(mux16n2t_2_out_15),
    .out_16(mux16n2t_2_out_16));
  Mux16N2T mux16n2t_3 (
    .a0(a_33), .b0(b_33), .a1(a_34), .b1(b_34), .a2(a_35), .b2(b_35), .a3(a_36), .b3(b_36), .a4(a_37),
    .b4(b_37), .a5(a_38), .b5(b_38), .a6(a_39), .b6(b_39), .a7(a_40), .sel(sel0), .b7(b_40), .a8(a_41),
    .b8(b_41), .a9(a_42), .b9(b_42), .a10(a_43), .b10(b_43), .a11(a_44), .b11(b_44), .a12(a_45), .b12(b_45),
    .a13(a_46), .b13(b_46), .a14(a_47), .b14(b_47), .a15(a_48), .b15(b_48), .out(mux16n2t_3_out),
    .out_2(mux16n2t_3_out_2), .out_3(mux16n2t_3_out_3), .out_4(mux16n2t_3_out_4), .out_5(mux16n2t_3_out_5),
    .out_6(mux16n2t_3_out_6), .out_7(mux16n2t_3_out_7), .out_8(mux16n2t_3_out_8), .out_9(mux16n2t_3_out_9),
    .out_10(mux16n2t_3_out_10), .out_11(mux16n2t_3_out_11), .out_12(mux16n2t_3_out_12),
    .out_13(mux16n2t_3_out_13), .out_14(mux16n2t_3_out_14), .out_15(mux16n2t_3_out_15),
    .out_16(mux16n2t_3_out_16));
  Mux16N2T mux16n2t_4 (
    .a0(a_49), .b0(b_49), .a1(a_50), .b1(b_50), .a2(a_51), .b2(b_51), .a3(a_52), .b3(b_52), .a4(a_53),
    .b4(b_53), .a5(a_54), .b5(b_54), .a6(a_55), .b6(b_55), .a7(a_56), .sel(sel0), .b7(b_56), .a8(a_57),
    .b8(b_57), .a9(a_58), .b9(b_58), .a10(a_59), .b10(b_59), .a11(a_60), .b11(b_60), .a12(a_61), .b12(b_61),
    .a13(a_62), .b13(b_62), .a14(a_63), .b14(b_63), .a15(a_64), .b15(b_64), .out(mux16n2t_4_out),
    .out_2(mux16n2t_4_out_2), .out_3(mux16n2t_4_out_3), .out_4(mux16n2t_4_out_4), .out_5(mux16n2t_4_out_5),
    .out_6(mux16n2t_4_out_6), .out_7(mux16n2t_4_out_7), .out_8(mux16n2t_4_out_8), .out_9(mux16n2t_4_out_9),
    .out_10(mux16n2t_4_out_10), .out_11(mux16n2t_4_out_11), .out_12(mux16n2t_4_out_12),
    .out_13(mux16n2t_4_out_13), .out_14(mux16n2t_4_out_14), .out_15(mux16n2t_4_out_15),
    .out_16(mux16n2t_4_out_16));
  Mux16N2T mux16n2t_5 (
    .a0(mux16n2t_1_out), .b0(mux16n2t_2_out), .a1(mux16n2t_1_out_2), .b1(mux16n2t_2_out_2),
    .a2(mux16n2t_1_out_3), .b2(mux16n2t_2_out_3), .a3(mux16n2t_1_out_4), .b3(mux16n2t_2_out_4),
    .a4(mux16n2t_1_out_5), .b4(mux16n2t_2_out_5), .a5(mux16n2t_1_out_6), .b5(mux16n2t_2_out_6),
    .a6(mux16n2t_1_out_7), .b6(mux16n2t_2_out_7), .a7(mux16n2t_1_out_8), .sel(sel1), .b7(mux16n2t_2_out_8),
    .a8(mux16n2t_1_out_9), .b8(mux16n2t_2_out_9), .a9(mux16n2t_1_out_10), .b9(mux16n2t_2_out_10),
    .a10(mux16n2t_1_out_11), .b10(mux16n2t_2_out_11), .a11(mux16n2t_1_out_12), .b11(mux16n2t_2_out_12),
    .a12(mux16n2t_1_out_13), .b12(mux16n2t_2_out_13), .a13(mux16n2t_1_out_14), .b13(mux16n2t_2_out_14),
    .a14(mux16n2t_1_out_15), .b14(mux16n2t_2_out_15), .a15(mux16n2t_1_out_16), .b15(mux16n2t_2_out_16),
    .out(mux16n2t_5_out), .out_2(mux16n2t_5_out_2), .out_3(mux16n2t_5_out_3), .out_4(mux16n2t_5_out_4),
    .out_5(mux16n2t_5_out_5), .out_6(mux16n2t_5_out_6), .out_7(mux16n2t_5_out_7), .out_8(mux16n2t_5_out_8),
    .out_9(mux16n2t_5_out_9), .out_10(mux16n2t_5_out_10), .out_11(mux16n2t_5_out_11),
    .out_12(mux16n2t_5_out_12), .out_13(mux16n2t_5_out_13), .out_14(mux16n2t_5_out_14),
    .out_15(mux16n2t_5_out_15), .out_16(mux16n2t_5_out_16));
  Mux16N2T mux16n2t_6 (
    .a0(mux16n2t_3_out), .b0(mux16n2t_4_out), .a1(mux16n2t_3_out_2), .b1(mux16n2t_4_out_2),
    .a2(mux16n2t_3_out_3), .b2(mux16n2t_4_out_3), .a3(mux16n2t_3_out_4), .b3(mux16n2t_4_out_4),
    .a4(mux16n2t_3_out_5), .b4(mux16n2t_4_out_5), .a5(mux16n2t_3_out_6), .b5(mux16n2t_4_out_6),
    .a6(mux16n2t_3_out_7), .b6(mux16n2t_4_out_7), .a7(mux16n2t_3_out_8), .sel(sel1), .b7(mux16n2t_4_out_8),
    .a8(mux16n2t_3_out_9), .b8(mux16n2t_4_out_9), .a9(mux16n2t_3_out_10), .b9(mux16n2t_4_out_10),
    .a10(mux16n2t_3_out_11), .b10(mux16n2t_4_out_11), .a11(mux16n2t_3_out_12), .b11(mux16n2t_4_out_12),
    .a12(mux16n2t_3_out_13), .b12(mux16n2t_4_out_13), .a13(mux16n2t_3_out_14), .b13(mux16n2t_4_out_14),
    .a14(mux16n2t_3_out_15), .b14(mux16n2t_4_out_15), .a15(mux16n2t_3_out_16), .b15(mux16n2t_4_out_16),
    .out(mux16n2t_6_out), .out_2(mux16n2t_6_out_2), .out_3(mux16n2t_6_out_3), .out_4(mux16n2t_6_out_4),
    .out_5(mux16n2t_6_out_5), .out_6(mux16n2t_6_out_6), .out_7(mux16n2t_6_out_7), .out_8(mux16n2t_6_out_8),
    .out_9(mux16n2t_6_out_9), .out_10(mux16n2t_6_out_10), .out_11(mux16n2t_6_out_11),
    .out_12(mux16n2t_6_out_12), .out_13(mux16n2t_6_out_13), .out_14(mux16n2t_6_out_14),
    .out_15(mux16n2t_6_out_15), .out_16(mux16n2t_6_out_16));
  Mux16N2T mux16n2t_7 (
    .a0(mux16n2t_5_out), .b0(mux16n2t_6_out), .a1(mux16n2t_5_out_2), .b1(mux16n2t_6_out_2),
    .a2(mux16n2t_5_out_3), .b2(mux16n2t_6_out_3), .a3(mux16n2t_5_out_4), .b3(mux16n2t_6_out_4),
    .a4(mux16n2t_5_out_5), .b4(mux16n2t_6_out_5), .a5(mux16n2t_5_out_6), .b5(mux16n2t_6_out_6),
    .a6(mux16n2t_5_out_7), .b6(mux16n2t_6_out_7), .a7(mux16n2t_5_out_8), .sel(sel2), .b7(mux16n2t_6_out_8),
    .a8(mux16n2t_5_out_9), .b8(mux16n2t_6_out_9), .a9(mux16n2t_5_out_10), .b9(mux16n2t_6_out_10),
    .a10(mux16n2t_5_out_11), .b10(mux16n2t_6_out_11), .a11(mux16n2t_5_out_12), .b11(mux16n2t_6_out_12),
    .a12(mux16n2t_5_out_13), .b12(mux16n2t_6_out_13), .a13(mux16n2t_5_out_14), .b13(mux16n2t_6_out_14),
    .a14(mux16n2t_5_out_15), .b14(mux16n2t_6_out_15), .a15(mux16n2t_5_out_16), .b15(mux16n2t_6_out_16),
    .out(out_132), .out_2(out_133), .out_3(out_134), .out_4(out_135), .out_5(out_136), .out_6(out_137),
    .out_7(out_138), .out_8(out_139), .out_9(out_140), .out_10(out_141), .out_11(out_142), .out_12(out_143),
    .out_13(out_144), .out_14(out_145), .out_15(out_146), .out_16(out_147));
endmodule

module DMux4WayN2T (
  input  in,
  input  sel1,
  input  in_3,
  output a,
  output b,
  output c,
  output d
);

  wire dmuxn2t_1_out, dmuxn2t_1_out_2;

  DMuxN2T dmuxn2t_1 (.in(in), .in_2(sel1), .out(dmuxn2t_1_out), .out_2(dmuxn2t_1_out_2));
  DMuxN2T dmuxn2t_2 (.in(dmuxn2t_1_out), .in_2(in_3), .out(a), .out_2(b));
  DMuxN2T dmuxn2t_3 (.in(dmuxn2t_1_out_2), .in_2(in_3), .out(c), .out_2(d));
endmodule

module DMux8WayN2T (
  input  in,
  input  sel2,
  input  in_3,
  input  in_4,
  output a,
  output b,
  output c,
  output d,
  output e,
  output f,
  output g,
  output h
);

  wire dmuxn2t_1_out, dmuxn2t_1_out_2, dmuxn2t_2_out, dmuxn2t_2_out_2, dmuxn2t_3_out, dmuxn2t_3_out_2;

  DMuxN2T dmuxn2t_1 (.in(in), .in_2(sel2), .out(dmuxn2t_1_out), .out_2(dmuxn2t_1_out_2));
  DMuxN2T dmuxn2t_2 (.in(dmuxn2t_1_out), .in_2(in_3), .out(dmuxn2t_2_out), .out_2(dmuxn2t_2_out_2));
  DMuxN2T dmuxn2t_3 (.in(dmuxn2t_1_out_2), .in_2(in_3), .out(dmuxn2t_3_out), .out_2(dmuxn2t_3_out_2));
  DMuxN2T dmuxn2t_4 (.in(dmuxn2t_2_out), .in_2(in_4), .out(a), .out_2(b));
  DMuxN2T dmuxn2t_5 (.in(dmuxn2t_2_out_2), .in_2(in_4), .out(c), .out_2(d));
  DMuxN2T dmuxn2t_6 (.in(dmuxn2t_3_out), .in_2(in_4), .out(e), .out_2(f));
  DMuxN2T dmuxn2t_7 (.in(dmuxn2t_3_out_2), .in_2(in_4), .out(g), .out_2(h));
endmodule
