// Logisim project alu.circ as structural Verilog: 5 circuits, main circuit HalfAdder
module HalfAdder (
  input  a,
  input  b,
  output sum,
  output carry
);

  xor xor_1 (sum, a, b);
  and and_1 (carry, a, b);
endmodule

module FullAdder (
  input  c,
  input  a,
  input  b,
  output sum,
  output carry
);

  wire halfadder_1_carry, halfadder_1_sum, halfadder_2_carry;

  HalfAdder halfadder_1 (.a(a), .b(b), .sum(halfadder_1_sum), .carry(halfadder_1_carry));
  HalfAdder halfadder_2 (.a(c), .b(halfadder_1_sum), .sum(sum), .carry(halfadder_2_carry));
  or or_1 (carry, halfadder_1_carry, halfadder_2_carry);
endmodule

module Inc16 (
  input  a,
  input  a_2,
  input  b,
  input  a_3,
  input  b_2,
  input  a_4,
  input  b_3,
  input  a_5,
  input  b_4,
  input  a_6,
  input  b_5,
  input  a_7,
  input  b_6,
  input  a_8,
  input  b_7,
  input  a_9,
  input  b_8,
  input  a_10,
  input  b_9,
  input  a_11,
  input  b_10,
  input  a_12,
  input  b_11,
  input  a_13,
  input  b_12,
  input  a_14,
  input  b_13,
  input  a_15,
  input  b_14,
  input  a_16,
  input  b_15,
  output out,
  output out_2,
  output out_3,
  output out_4,
  output out_5,
  output out_6,
  output out_7,
  output out_8,
  output out_9,
  output out_10,
  output out_11,
  output out_12,
  output out_13,
  output out_14,
  output out_15,
  output out_16
);

  Add16 add16_1 (
    .a(a), .b(1'b1), .a_2(a_2), .b_2(b), .a_3(a_3), .b_3(b_2), .a_4(a_4), .b_4(b_3), .a_5(a_5), .b_5(b_4),
    .a_6(a_6), .b_6(b_5), .a_7(a_7), .b_7(b_6), .a_8(a_8), .b_8(b_7), .a_9(a_9), .b_9(b_8), .a_10(a_10),
    .b_10(b_9), .a_11(a_11), .b_11(b_10), .a_12(a_12), .b_12(b_11), .a_13(a_13), .b_13(b_12), .a_14(a_14),
    .b_14(b_13), .a_15(a_15), .b_15(b_14), .a_16(a_16), .b_16(b_15), .out(out), .out_2(out_2), .out_3(out_3),
    .out_4(out_4), .out_5(out_5), .out_6(out_6), .out_7(out_7), .out_8(out_8), .out_9(out_9),
    .out_10(out_10), .out_11(out_11), .out_12(out_12), .out_13(out_13), .out_14(out_14), .out_15(out_15),
    .out_16(out_16));
endmodule

module Add16 (
  input  a,
  input  b,
  input  a_2,
  input  b_2,
  input  a_3,
  input  b_3,
  input  a_4,
  input  b_4,
  input  a_5,
  input  b_5,
  input  a_6,
  input  b_6,
  input  a_7,
  input  b_7,
  input  a_8,
  input  b_8,
  input  a_9,
  input  b_9,
  input  a_10,
  input  b_10,
  input  a_11,
  input  b_11,
  input  a_12,
  input  b_12,
  input  a_13,
  input  b_13,
  input  a_14,
  input  b_14,
  input  a_15,
  input  b_15,
  input  a_16,
  input  b_16,
  output out,
  output out_2,
  output out_3,
  output out_4,
  output out_5,
  output out_6,
  output out_7,
  output out_8,
  output out_9,
  output out_10,
  output out_11,
  output out_12,
  output out_13,
  output out_14,
  output out_15,
  output out_16
);

  wire FullAdder_2_carry, FullAdder_3_carry, FullAdder_4_carry, FullAdder_5_carry, FullAdder_6_carry,
       FullAdder_7_carry, FullAdder_8_carry, FullAdder_9_carry, FullAdder_10_carry, FullAdder_11_carry,
       FullAdder_12_carry, FullAdder_13_carry, FullAdder_14_carry, FullAdder_carry, HalfAdder_carry;

  HalfAdder HalfAdder (.a(a_16), .b(b_16), .sum(out_16), .carry(HalfAdder_carry));
  FullAdder FullAdder (.c(a_15), .a(b_15), .b(HalfAdder_carry), .sum(out_15), .carry(FullAdder_carry));
  FullAdder FullAdder_2 (.c(a_14), .a(b_14), .b(FullAdder_carry), .sum(out_14), .carry(FullAdder_2_carry));
  FullAdder FullAdder_3 (.c(a_13), .a(b_13), .b(FullAdder_2_carry), .sum(out_13), .carry(FullAdder_3_carry));
  FullAdder FullAdder_4 (.c(a_12), .a(b_12), .b(FullAdder_3_carry), .sum(out_12), .carry(FullAdder_4_carry));
  FullAdder FullAdder_5 (.c(a_11), .a(b_11), .b(FullAdder_4_carry), .sum(out_11), .carry(FullAdder_5_carry));
  FullAdder FullAdder_6 (.c(a_10), .a(b_10), .b(FullAdder_5_carry), .sum(out_10), .carry(FullAdder_6_carry));
  FullAdder FullAdder_7 (.c(a_9), .a(b_9), .b(FullAdder_6_carry), .sum(out_9), .carry(FullAdder_7_carry));
  FullAdder FullAdder_8 (.c(a_8), .a(b_8), .b(FullAdder_7_carry), .sum(out_8), .carry(FullAdder_8_carry));
  FullAdder FullAdder_9 (.c(a_7), .a(b_7), .b(FullAdder_8_carry), .sum(out_7), .carry(FullAdder_9_carry));
  FullAdder FullAdder_10 (.c(a_6), .a(b_6), .b(FullAdder_9_carry), .sum(out_6), .carry(FullAdder_10_carry));
  FullAdder FullAdder_11 (.c(a_5), .a(b_5), .b(FullAdder_10_carry), .sum(out_5), .carry(FullAdder_11_carry));
  FullAdder FullAdder_12 (.c(a_4), .a(b_4), .b(FullAdder_11_carry), .sum(out_4), .carry(FullAdder_12_carry));
  FullAdder FullAdder_13 (.c(a_3), .a(b_3), .b(FullAdder_12_carry), .sum(out_3), .carry(FullAdder_13_carry));
  FullAdder FullAdder_14 (.c(a_2), .a(b_2), .b(FullAdder_13_carry), .sum(out_2), .carry(FullAdder_14_carry));
  FullAdder FullAdder_15 (.c(a), .a(b), .b(FullAdder_14_carry), .sum(out));  // open: carry
endmodule

module ALU (
  input  [15:0] x,
  input  nx,
  input  zx,
  input  no,
  input  [15:0] y,
  input  f,
  input  ny,
  input  zy,
  input  in_9,
  output zr,
  output ng,
  output [15:0] out_12
);

  wire or_1_out, or_2_out, or_3_out;
  wire [15:0] adder_1_out, and_1_out, multiplexer_1_out, multiplexer_2_out, multiplexer_3_out,
       multiplexer_4_out, multiplexer_5_out, not_1_out, not_2_out, not_3_out;

  Multiplexer #(.width(16)) multiplexer_1 (.in0(x), .in1({16{1'b0}}), .out(multiplexer_1_out), .sel(zx));  // open: en
  Multiplexer #(.width(16)) multiplexer_2 (.in0(y), .in1({16{1'b0}}), .out(multiplexer_2_out), .sel(zy));  // open: en
  assign not_1_out = ~multiplexer_1_out;  // NOT_Gate not_1, 16 bits wide
  assign not_2_out = ~multiplexer_2_out;  // NOT_Gate not_2, 16 bits wide
  Multiplexer #(.width(16)) multiplexer_3 (
    .in0(multiplexer_1_out), .in1(not_1_out), .out(multiplexer_3_out), .sel(nx));  // open: en
  Multiplexer #(.width(16)) multiplexer_4 (
    .in0(multiplexer_2_out), .in1(not_2_out), .out(multiplexer_4_out), .sel(ny));  // open: en
  assign and_1_out = multiplexer_3_out & multiplexer_4_out;  // AND_Gate and_1, 16 bits wide
  Adder #(.width(16)) adder_1 (.a(multiplexer_3_out), .b(multiplexer_4_out), .out(adder_1_out));  // open: cin, cout
  Multiplexer #(.width(16)) multiplexer_5 (
    .in0(adder_1_out), .in1(and_1_out), .out(multiplexer_5_out), .sel(f));  // open: en
  assign not_3_out = ~multiplexer_5_out;  // NOT_Gate not_3, 16 bits wide
  Multiplexer #(.width(16)) multiplexer_6 (
    .in0(multiplexer_5_out), .in1(not_3_out), .out({ng, out_12[14:0]}), .sel(no));  // open: en
  or or_1 (or_1_out, out_12[0], out_12[1], out_12[2], out_12[3], out_12[4], out_12[5], out_12[6], out_12[7]);
  or or_2 (or_2_out, out_12[8], out_12[9], out_12[10], out_12[11], out_12[12], out_12[13], out_12[14], ng);
  or or_3 (or_3_out, or_1_out, or_2_out);
  not not_4 (zr, or_3_out);

  assign out_12[15] = ng;
endmodule
