// Logisim project proyecto03.circ as structural Verilog: 6 circuits, main circuit Bit
module Bit (
  input  in,
  input  load,
  output out
);

  wire clock_1_out, multiplexer_1_out;

  Clock clock_1 (.out(clock_1_out));
  Multiplexer multiplexer_1 (.in0(out), .in1(in), .out(multiplexer_1_out), .sel(load));  // open: en
  D_Flip_Flop d_ff_1 (.clk(clock_1_out), .D(multiplexer_1_out), .Q(out));  // open: Qn, preset, en, reset
endmodule

module Register (
  input  [15:0] in,
  input  load,
  output [15:0] out
);

  Bit bit_1 (.in(in[0]), .load(load), .out(out[0]));
  Bit bit_2 (.in(in[1]), .load(load), .out(out[1]));
  Bit bit_3 (.in(in[2]), .load(load), .out(out[2]));
  Bit bit_4 (.in(in[3]), .load(load), .out(out[3]));
  Bit bit_5 (.in(in[4]), .load(load), .out(out[4]));
  Bit bit_6 (.in(in[5]), .load(load), .out(out[5]));
  Bit bit_7 (.in(in[6]), .load(load), .out(out[6]));
  Bit bit_8 (.in(in[7]), .load(load), .out(out[7]));
  Bit bit_9 (.in(in[8]), .load(load), .out(out[8]));
  Bit bit_10 (.in(in[9]), .load(load), .out(out[9]));
  Bit bit_11 (.in(in[10]), .load(load), .out(out[10]));
  Bit bit_12 (.in(in[11]), .load(load), .out(out[11]));
  Bit bit_13 (.in(in[12]), .load(load), .out(out[12]));
  Bit bit_14 (.in(in[13]), .load(load), .out(out[13]));
  Bit bit_15 (.in(in[14]), .load(load), .out(out[14]));
  Bit bit_16 (.in(in[15]), .load(load), .out(out[15]));
endmodule

module RAM8 (
  input  [15:0] in,
  input  load,
  input  [2:0] address,
  output [15:0] out
);

  wire demultiplexer_1_out0, demultiplexer_1_out1, demultiplexer_1_out2, demultiplexer_1_out3,
       demultiplexer_1_out4, demultiplexer_1_out5, demultiplexer_1_out6, demultiplexer_1_out7;
  wire [15:0] register_1_out, register_2_out, register_3_out, register_4_out, register_5_out, register_6_out,
       register_7_out, register_8_out;

  Demultiplexer #(.select(3)) demultiplexer_1 (
    .out0(demultiplexer_1_out0), .out1(demultiplexer_1_out1), .out2(demultiplexer_1_out2),
    .out3(demultiplexer_1_out3), .out4(demultiplexer_1_out4), .out5(demultiplexer_1_out5),
    .out6(demultiplexer_1_out6), .out7(demultiplexer_1_out7), .in(load), .sel(address));  // open: en
  Register register_1 (.in(in), .load(demultiplexer_1_out0), .out(register_1_out));
  Register register_2 (.in(in), .load(demultiplexer_1_out1), .out(register_2_out));
  Register register_3 (.in(in), .load(demultiplexer_1_out2), .out(register_3_out));
  Register register_4 (.in(in), .load(demultiplexer_1_out3), .out(register_4_out));
  Register register_5 (.in(in), .load(demultiplexer_1_out4), .out(register_5_out));
  Register register_6 (.in(in), .load(demultiplexer_1_out5), .out(register_6_out));
  Register register_7 (.in(in), .load(demultiplexer_1_out6), .out(register_7_out));
  Register register_8 (.in(in), .load(demultiplexer_1_out7), .out(register_8_out));
  Multiplexer #(.select(3), .width(16)) multiplexer_1 (
    .in0(register_1_out), .in1(register_2_out), .in2(register_3_out), .in3(register_4_out),
    .in4(register_5_out), .in5(register_6_out), .in6(register_7_out), .in7(register_8_out), .out(out),
    .sel(address));  // open: en
endmodule

module RAM64 (
  input  [15:0] in,
  input  load,
  input  [5:0] address,
  output [15:0] out_4
);

  wire demultiplexer_1_out0, demultiplexer_1_out1, demultiplexer_1_out2, demultiplexer_1_out3,
       demultiplexer_1_out4, demultiplexer_1_out5, demultiplexer_1_out6, demultiplexer_1_out7;
  wire [15:0] ram8_1_out, ram8_2_out, ram8_3_out, ram8_4_out, ram8_5_out, ram8_6_out, ram8_7_out, ram8_8_out;

  Demultiplexer #(.select(3)) demultiplexer_1 (
    .out0(demultiplexer_1_out0), .out1(demultiplexer_1_out1), .out2(demultiplexer_1_out2),
    .out3(demultiplexer_1_out3), .out4(demultiplexer_1_out4), .out5(demultiplexer_1_out5),
    .out6(demultiplexer_1_out6), .out7(demultiplexer_1_out7), .in(load), .sel(address[2:0]));  // open: en
  RAM8 ram8_1 (.in(in), .load(demultiplexer_1_out0), .address(address[5:3]), .out(ram8_1_out));
  RAM8 ram8_2 (.in(in), .load(demultiplexer_1_out1), .address(address[5:3]), .out(ram8_2_out));
  RAM8 ram8_3 (.in(in), .load(demultiplexer_1_out6), .address(address[5:3]), .out(ram8_3_out));
  RAM8 ram8_4 (.in(in), .load(demultiplexer_1_out7), .address(address[5:3]), .out(ram8_4_out));
  RAM8 ram8_5 (.in(in), .load(demultiplexer_1_out2), .address(address[5:3]), .out(ram8_5_out));
  RAM8 ram8_6 (.in(in), .load(demultiplexer_1_out3), .address(address[5:3]), .out(ram8_6_out));
  RAM8 ram8_7 (.in(in), .load(demultiplexer_1_out4), .address(address[5:3]), .out(ram8_7_out));
  RAM8 ram8_8 (.in(in), .load(demultiplexer_1_out5), .address(address[5:3]), .out(ram8_8_out));
  Multiplexer #(.select(3), .width(16)) multiplexer_1 (
    .in0(ram8_1_out), .in1(ram8_2_out), .in2(ram8_5_out), .in3(ram8_6_out), .in4(ram8_7_out),
    .in5(ram8_8_out), .in6(ram8_3_out), .in7(ram8_4_out), .out(out_4), .sel(address[2:0]));  // open: en

  // Other names for the same wires on the sheet: dm[2:0] = address[2:0]; rm[2:0] = address[5:3]
endmodule

module PC (
  input  inc,
  input  reset,
  input  [15:0] in,
  input  load,
  output [15:0] out_5
);

  wire [15:0] inc16_1_out, multiplexer_1_out, multiplexer_2_out, multiplexer_3_out;

  INC16 inc16_1 (.in(out_5), .out(inc16_1_out));
  Multiplexer #(.width(16)) multiplexer_1 (
    .in0(out_5), .in1(inc16_1_out), .out(multiplexer_1_out), .sel(inc));  // open: en
  Multiplexer #(.width(16)) multiplexer_2 (
    .in0(multiplexer_1_out), .in1(in), .out(multiplexer_2_out), .sel(load));  // open: en
  Multiplexer #(.width(16)) multiplexer_3 (
    .in0(multiplexer_2_out), .in1({16{1'b0}}), .out(multiplexer_3_out), .sel(reset));  // open: en
  Register register_1 (.in(multiplexer_3_out), .load(1'b1), .out(out_5));
endmodule

module INC16 (
  input  [15:0] in,
  output [15:0] out
);

  Adder #(.width(16)) adder_1 (.a(in), .b(16'h1), .out(out));  // open: cin, cout
endmodule
