// Logisim project Proyecto01.circ as structural Verilog: 15 circuits, main circuit AndNT
module AndNT (
  input  in_1,
  input  in_2,
  output out_3
);

  wire nand_1_out;

  nand nand_1 (nand_1_out, in_1, in_2);
  NotN2T notn2t_1 (.in(nand_1_out), .out(out_3));
endmodule

module NotN2T (
  input  in,
  output out
);

  nand nand_1 (out, in, in);
endmodule

module ORN2T (
  input  in_1,
  input  in_2,
  output out_3
);

  wire notn2t_1_out, notn2t_2_out;

  NotN2T notn2t_1 (.in(in_1), .out(notn2t_1_out));
  NotN2T notn2t_2 (.in(in_2), .out(notn2t_2_out));
  nand nand_1 (out_3, notn2t_1_out, notn2t_2_out);
endmodule

module XORN2T (
  input  A,
  input  B,
  output out_3
);

  wire andnt_1_out_3, andnt_2_out_3, notn2t_1_out, notn2t_2_out;

  NotN2T notn2t_1 (.in(A), .out(notn2t_1_out));
  NotN2T notn2t_2 (.in(B), .out(notn2t_2_out));
  AndNT andnt_1 (.in_1(A), .in_2(notn2t_2_out), .out_3(andnt_1_out_3));
  AndNT andnt_2 (.in_1(notn2t_1_out), .in_2(B), .out_3(andnt_2_out_3));
  ORN2T orn2t_1 (.in_1(andnt_1_out_3), .in_2(andnt_2_out_3), .out_3(out_3));
endmodule

module Mux2T (
  input  SEL,
  input  A,
  input  B,
  output out_4
);

  wire andnt_1_out_3, andnt_2_out_3, notn2t_1_out;

  NotN2T notn2t_1 (.in(SEL), .out(notn2t_1_out));
  AndNT andnt_1 (.in_1(A), .in_2(notn2t_1_out), .out_3(andnt_1_out_3));
  AndNT andnt_2 (.in_1(B), .in_2(SEL), .out_3(andnt_2_out_3));
  ORN2T orn2t_1 (.in_1(andnt_1_out_3), .in_2(andnt_2_out_3), .out_3(out_4));
endmodule

module DMUX2T (
  input  IN,
  input  SEL,
  output A,
  output B
);

  wire notn2t_1_out;

  NotN2T notn2t_1 (.in(SEL), .out(notn2t_1_out));
  AndNT andnt_1 (.in_1(IN), .in_2(notn2t_1_out), .out_3(A));
  AndNT andnt_2 (.in_1(IN), .in_2(SEL), .out_3(B));
endmodule

module NOT16 (
  input  [15:0] IN,
  output [15:0] OUT
);

  NotN2T notn2t_1 (.in(IN[0]), .out(OUT[0]));
  NotN2T notn2t_2 (.in(IN[1]), .out(OUT[1]));
  NotN2T notn2t_3 (.in(IN[2]), .out(OUT[2]));
  NotN2T notn2t_4 (.in(IN[3]), .out(OUT[3]));
  NotN2T notn2t_5 (.in(IN[4]), .out(OUT[4]));
  NotN2T notn2t_6 (.in(IN[5]), .out(OUT[5]));
  NotN2T notn2t_7 (.in(IN[6]), .out(OUT[6]));
  NotN2T notn2t_8 (.in(IN[7]), .out(OUT[7]));
  NotN2T notn2t_9 (.in(IN[8]), .out(OUT[8]));
  NotN2T notn2t_10 (.in(IN[9]), .out(OUT[9]));
  NotN2T notn2t_11 (.in(IN[10]), .out(OUT[10]));
  NotN2T notn2t_12 (.in(IN[11]), .out(OUT[11]));
  NotN2T notn2t_13 (.in(IN[12]), .out(OUT[12]));
  NotN2T notn2t_14 (.in(IN[13]), .out(OUT[13]));
  NotN2T notn2t_15 (.in(IN[14]), .out(OUT[14]));
  NotN2T notn2t_16 (.in(IN[15]), .out(OUT[15]));
endmodule

module AND16 (
  input  A0,
  input  B0,
  input  A1,
  input  B1,
  input  A2,
  input  B2,
  input  A3,
  input  B3,
  input  A4,
  input  B4,
  input  A5,
  input  B5,
  input  A6,
  input  B6,
  input  A7,
  input  B7,
  input  A8,
  input  B8,
  input  A9,
  input  B9,
  input  A10,
  input  B10,
  input  A11,
  input  B11,
  input  A12,
  input  B12,
  input  A13,
  input  B13,
  input  A14,
  input  B14,
  input  A15,
  input  B15,
  output [15:0] out_33
);

  AndNT andnt_1 (.in_1(A0), .in_2(B0), .out_3(out_33[0]));
  AndNT andnt_2 (.in_1(A1), .in_2(B1), .out_3(out_33[1]));
  AndNT andnt_3 (.in_1(A2), .in_2(B2), .out_3(out_33[2]));
  AndNT andnt_4 (.in_1(A3), .in_2(B3), .out_3(out_33[3]));
  AndNT andnt_5 (.in_1(A4), .in_2(B4), .out_3(out_33[4]));
  AndNT andnt_6 (.in_1(A5), .in_2(B5), .out_3(out_33[5]));
  AndNT andnt_7 (.in_1(A6), .in_2(B6), .out_3(out_33[6]));
  AndNT andnt_8 (.in_1(A7), .in_2(B7), .out_3(out_33[7]));
  AndNT andnt_9 (.in_1(A8), .in_2(B8), .out_3(out_33[8]));
  AndNT andnt_10 (.in_1(A9), .in_2(B9), .out_3(out_33[9]));
  AndNT andnt_11 (.in_1(A10), .in_2(B10), .out_3(out_33[10]));
  AndNT andnt_12 (.in_1(A11), .in_2(B11), .out_3(out_33[11]));
  AndNT andnt_13 (.in_1(A12), .in_2(B12), .out_3(out_33[12]));
  AndNT andnt_14 (.in_1(A13), .in_2(B13), .out_3(out_33[13]));
  AndNT andnt_15 (.in_1(A14), .in_2(B14), .out_3(out_33[14]));
  AndNT andnt_16 (.in_1(A15), .in_2(B15), .out_3(out_33[15]));
endmodule

module OR16 (
  input  A0,
  input  B0,
  input  A1,
  input  B1,
  input  A2,
  input  B2,
  input  A3,
  input  B3,
  input  A4,
  input  B4,
  input  A5,
  input  B5,
  input  A6,
  input  B6,
  input  A7,
  input  B7,
  input  A8,
  input  B8,
  input  A9,
  input  B9,
  input  A10,
  input  B10,
  input  A11,
  input  B11,
  input  A12,
  input  B12,
  input  A13,
  input  B13,
  input  A14,
  input  B14,
  input  A15,
  input  B15,
  output [15:0] out_33
);

  ORN2T orn2t_1 (.in_1(A0), .in_2(B0), .out_3(out_33[0]));
  ORN2T orn2t_2 (.in_1(A1), .in_2(B1), .out_3(out_33[1]));
  ORN2T orn2t_3 (.in_1(A2), .in_2(B2), .out_3(out_33[2]));
  ORN2T orn2t_4 (.in_1(A3), .in_2(B3), .out_3(out_33[3]));
  ORN2T orn2t_5 (.in_1(A4), .in_2(B4), .out_3(out_33[4]));
  ORN2T orn2t_6 (.in_1(A5), .in_2(B5), .out_3(out_33[5]));
  ORN2T orn2t_7 (.in_1(A6), .in_2(B6), .out_3(out_33[6]));
  ORN2T orn2t_8 (.in_1(A7), .in_2(B7), .out_3(out_33[7]));
  ORN2T orn2t_9 (.in_1(A8), .in_2(B8), .out_3(out_33[8]));
  ORN2T orn2t_10 (.in_1(A9), .in_2(B9), .out_3(out_33[9]));
  ORN2T orn2t_11 (.in_1(A10), .in_2(B10), .out_3(out_33[10]));
  ORN2T orn2t_12 (.in_1(A11), .in_2(B11), .out_3(out_33[11]));
  ORN2T orn2t_13 (.in_1(A12), .in_2(B12), .out_3(out_33[12]));
  ORN2T orn2t_14 (.in_1(A13), .in_2(B13), .out_3(out_33[13]));
  ORN2T orn2t_15 (.in_1(A14), .in_2(B14), .out_3(out_33[14]));
  ORN2T orn2t_16 (.in_1(A15), .in_2(B15), .out_3(out_33[15]));
endmodule

module MUX16 (
  input  SEL,
  input  A0,
  input  B0,
  input  A1,
  input  B1,
  input  A2,
  input  B2,
  input  A3,
  input  B3,
  input  A4,
  input  B4,
  input  A5,
  input  B5,
  input  A6,
  input  B6,
  input  A7,
  input  B7,
  input  A8,
  input  B8,
  input  A9,
  input  B9,
  input  A10,
  input  B10,
  input  A11,
  input  B11,
  input  A12,
  input  B12,
  input  A13,
  input  B13,
  input  A14,
  input  B14,
  input  A15,
  input  B15,
  output out_34,
  output out_35,
  output out_36,
  output out_37,
  output out_38,
  output out_39,
  output out_40,
  output out_41,
  output out_42,
  output out_43,
  output out_44,
  output out_45,
  output out_46,
  output out_47,
  output out_48,
  output out_49
);

  Mux2T mux2t_1 (.SEL(SEL), .A(A0), .B(B0), .out_4(out_34));
  Mux2T mux2t_2 (.SEL(SEL), .A(A1), .B(B1), .out_4(out_35));
  Mux2T mux2t_3 (.SEL(SEL), .A(A2), .B(B2), .out_4(out_36));
  Mux2T mux2t_4 (.SEL(SEL), .A(A3), .B(B3), .out_4(out_37));
  Mux2T mux2t_5 (.SEL(SEL), .A(A4), .B(B4), .out_4(out_38));
  Mux2T mux2t_6 (.SEL(SEL), .A(A5), .B(B5), .out_4(out_39));
  Mux2T mux2t_7 (.SEL(SEL), .A(A6), .B(B6), .out_4(out_40));
  Mux2T mux2t_8 (.SEL(SEL), .A(A7), .B(B7), .out_4(out_41));
  Mux2T mux2t_9 (.SEL(SEL), .A(A8), .B(B8), .out_4(out_42));
  Mux2T mux2t_10 (.SEL(SEL), .A(A9), .B(B9), .out_4(out_43));
  Mux2T mux2t_11 (.SEL(SEL), .A(A10), .B(B10), .out_4(out_44));
  Mux2T mux2t_12 (.SEL(SEL), .A(A11), .B(B11), .out_4(out_45));
  Mux2T mux2t_13 (.SEL(SEL), .A(A12), .B(B12), .out_4(out_46));
  Mux2T mux2t_14 (.SEL(SEL), .A(A13), .B(B13), .out_4(out_47));
  Mux2T mux2t_15 (.SEL(SEL), .A(A14), .B(B14), .out_4(out_48));
  Mux2T mux2t_16 (.SEL(SEL), .A(A15), .B(B15), .out_4(out_49));
endmodule

module OR8WAY (
  input  in_1,
  input  in_2,
  input  in_3,
  input  in_4,
  input  in_5,
  input  in_6,
  input  in_7,
  input  in_8,
  output out_9
);

  wire orn2t_1_out_3, orn2t_2_out_3, orn2t_3_out_3, orn2t_4_out_3, orn2t_5_out_3, orn2t_6_out_3;

  ORN2T orn2t_1 (.in_1(in_1), .in_2(in_2), .out_3(orn2t_1_out_3));
  ORN2T orn2t_2 (.in_1(in_3), .in_2(in_4), .out_3(orn2t_2_out_3));
  ORN2T orn2t_3 (.in_1(in_5), .in_2(in_6), .out_3(orn2t_3_out_3));
  ORN2T orn2t_4 (.in_1(in_7), .in_2(in_8), .out_3(orn2t_4_out_3));
  ORN2T orn2t_5 (.in_1(orn2t_1_out_3), .in_2(orn2t_2_out_3), .out_3(orn2t_5_out_3));
  ORN2T orn2t_6 (.in_1(orn2t_3_out_3), .in_2(orn2t_4_out_3), .out_3(orn2t_6_out_3));
  ORN2T orn2t_7 (.in_1(orn2t_5_out_3), .in_2(orn2t_6_out_3), .out_3(out_9));
endmodule

module MUX4WAY16 (
  input  SEL,
  input  A0,
  input  B0,
  input  A1,
  input  B1,
  input  A2,
  input  B2,
  input  A3,
  input  B3,
  input  A4,
  input  B4,
  input  A5,
  input  B5,
  input  A6,
  input  B6,
  input  A7,
  input  B7,
  input  A8,
  input  B8,
  input  A9,
  input  B9,
  input  A10,
  input  B10,
  input  A11,
  input  B11,
  input  A12,
  input  B12,
  input  A13,
  input  B13,
  input  A14,
  input  B14,
  input  A15,
  input  B15,
  input  in_34,
  input  in_35,
  input  in_36,
  input  in_37,
  input  in_38,
  input  in_39,
  input  in_40,
  input  in_41,
  input  in_42,
  input  in_43,
  input  in_44,
  input  in_45,
  input  in_46,
  input  in_47,
  input  in_48,
  input  in_49,
  input  in_50,
  input  in_51,
  input  in_52,
  input  in_53,
  input  in_54,
  input  in_55,
  input  in_56,
  input  in_57,
  input  in_58,
  input  in_59,
  input  in_60,
  input  in_61,
  input  in_62,
  input  in_63,
  input  in_64,
  input  in_65,
  input  SEL1,
  output out_67,
  output out_68,
  output out_69,
  output out_70,
  output out_71,
  output out_72,
  output out_73,
  output out_74,
  output out_75,
  output out_76,
  output out_77,
  output out_78,
  output out_79,
  output out_80,
  output out_81,
  output out_82
);

  wire mux16_1_out_34, mux16_1_out_35, mux16_1_out_36, mux16_1_out_37, mux16_1_out_38, mux16_1_out_39,
       mux16_1_out_40, mux16_1_out_41, mux16_1_out_42, mux16_1_out_43, mux16_1_out_44, mux16_1_out_45,
       mux16_1_out_46, mux16_1_out_47, mux16_1_out_48, mux16_1_out_49, mux16_2_out_34, mux16_2_out_35,
       mux16_2_out_36, mux16_2_out_37, mux16_2_out_38, mux16_2_out_39, mux16_2_out_40, mux16_2_out_41,
       mux16_2_out_42, mux16_2_out_43, mux16_2_out_44, mux16_2_out_45, mux16_2_out_46, mux16_2_out_47,
       mux16_2_out_48, mux16_2_out_49;

  MUX16 mux16_1 (
    .SEL(SEL), .A0(A0), .B0(B0), .A1(A1), .B1(B1), .A2(A2), .B2(B2), .A3(A3), .B3(B3), .A4(A4), .B4(B4),
    .A5(A5), .B5(B5), .A6(A6), .B6(B6), .A7(A7), .B7(B7), .A8(A8), .B8(B8), .A9(A9), .B9(B9), .A10(A10),
    .B10(B10), .A11(A11), .B11(B11), .A12(A12), .B12(B12), .A13(A13), .B13(B13), .A14(A14), .B14(B14),
    .A15(A15), .B15(B15), .out_34(mux16_1_out_34), .out_35(mux16_1_out_35), .out_36(mux16_1_out_36),
    .out_37(mux16_1_out_37), .out_38(mux16_1_out_38), .out_39(mux16_1_out_39), .out_40(mux16_1_out_40),
    .out_41(mux16_1_out_41), .out_42(mux16_1_out_42), .out_43(mux16_1_out_43), .out_44(mux16_1_out_44),
    .out_45(mux16_1_out_45), .out_46(mux16_1_out_46), .out_47(mux16_1_out_47), .out_48(mux16_1_out_48),
    .out_49(mux16_1_out_49));
  MUX16 mux16_2 (
    .SEL(SEL), .A0(in_34), .B0(in_35), .A1(in_36), .B1(in_37), .A2(in_38), .B2(in_39), .A3(in_40),
    .B3(in_41), .A4(in_42), .B4(in_43), .A5(in_44), .B5(in_45), .A6(in_46), .B6(in_47), .A7(in_48),
    .B7(in_49), .A8(in_50), .B8(in_51), .A9(in_52), .B9(in_53), .A10(in_54), .B10(in_55), .A11(in_56),
    .B11(in_57), .A12(in_58), .B12(in_59), .A13(in_60), .B13(in_61), .A14(in_62), .B14(in_63), .A15(in_64),
    .B15(in_65), .out_34(mux16_2_out_34), .out_35(mux16_2_out_35), .out_36(mux16_2_out_36),
    .out_37(mux16_2_out_37), .out_38(mux16_2_out_38), .out_39(mux16_2_out_39), .out_40(mux16_2_out_40),
    .out_41(mux16_2_out_41), .out_42(mux16_2_out_42), .out_43(mux16_2_out_43), .out_44(mux16_2_out_44),
    .out_45(mux16_2_out_45), .out_46(mux16_2_out_46), .out_47(mux16_2_out_47), .out_48(mux16_2_out_48),
    .out_49(mux16_2_out_49));
  MUX16 mux16_3 (
    .SEL(SEL1), .A0(mux16_1_out_34), .B0(mux16_2_out_34), .A1(mux16_1_out_35), .B1(mux16_2_out_35),
    .A2(mux16_1_out_36), .B2(mux16_2_out_36), .A3(mux16_1_out_37), .B3(mux16_2_out_37), .A4(mux16_1_out_38),
    .B4(mux16_2_out_38), .A5(mux16_1_out_39), .B5(mux16_2_out_39), .A6(mux16_1_out_40), .B6(mux16_2_out_40),
    .A7(mux16_1_out_41), .B7(mux16_2_out_41), .A8(mux16_1_out_42), .B8(mux16_2_out_42), .A9(mux16_1_out_43),
    .B9(mux16_2_out_43), .A10(mux16_1_out_44), .B10(mux16_2_out_44), .A11(mux16_1_out_45),
    .B11(mux16_2_out_45), .A12(mux16_1_out_46), .B12(mux16_2_out_46), .A13(mux16_1_out_47),
    .B13(mux16_2_out_47), .A14(mux16_1_out_48), .B14(mux16_2_out_48), .A15(mux16_1_out_49),
    .B15(mux16_2_out_49), .out_34(out_67), .out_35(out_68), .out_36(out_69), .out_37(out_70),
    .out_38(out_71), .out_39(out_72), .out_40(out_73), .out_41(out_74), .out_42(out_75), .out_43(out_76),
    .out_44(out_77), .out_45(out_78), .out_46(out_79), .out_47(out_80), .out_48(out_81), .out_49(out_82));
endmodule

module Mux8Way16 (
  input  in_1,
  input  in_2,
  input  in_3,
  input  in_4,
  input  in_5,
  input  in_6,
  input  in_7,
  input  in_8,
  input  in_9,
  input  in_10,
  input  in_11,
  input  in_12,
  input  in_13,
  input  in_14,
  input  in_15,
  input  in_16,
  input  in_17,
  input  in_18,
  input  in_19,
  input  in_20,
  input  in_21,
  input  in_22,
  input  in_23,
  input  in_24,
  input  in_25,
  input  in_26,
  input  in_27,
  input  in_28,
  input  in_29,
  input  in_30,
  input  in_31,
  input  in_32,
  input  in_33,
  input  in_34,
  input  in_35,
  input  in_36,
  input  in_37,
  input  in_38,
  input  in_39,
  input  in_40,
  input  in_41,
  input  in_42,
  input  in_43,
  input  in_44,
  input  in_45,
  input  in_46,
  input  in_47,
  input  in_48,
  input  in_49,
  input  in_50,
  input  in_51,
  input  in_52,
  input  in_53,
  input  in_54,
  input  in_55,
  input  in_56,
  input  in_57,
  input  in_58,
  input  in_59,
  input  SEL2,
  input  in_61,
  input  in_62,
  input  in_63,
  input  in_64,
  input  SEL0,
  input  in_66,
  input  SEL1,
  input  in_68,
  input  in_69,
  input  in_70,
  input  in_71,
  input  in_72,
  input  in_73,
  input  in_74,
  input  in_75,
  input  in_76,
  input  in_77,
  input  in_78,
  input  in_79,
  input  in_80,
  input  in_81,
  input  in_82,
  input  in_83,
  input  in_84,
  input  in_85,
  input  in_86,
  input  in_87,
  input  in_88,
  input  in_89,
  input  in_90,
  input  in_91,
  input  in_92,
  input  in_93,
  input  in_94,
  input  in_95,
  input  in_96,
  input  in_97,
  input  in_98,
  input  in_99,
  input  in_100,
  input  in_101,
  input  in_102,
  input  in_103,
  input  in_104,
  input  in_105,
  input  in_106,
  input  in_107,
  input  in_108,
  input  in_109,
  input  in_110,
  input  in_111,
  input  in_112,
  input  in_113,
  input  in_114,
  input  in_115,
  input  in_116,
  input  in_117,
  input  in_118,
  input  in_119,
  input  in_120,
  input  in_121,
  input  in_122,
  input  in_123,
  input  in_124,
  input  in_125,
  input  in_126,
  input  in_127,
  input  in_128,
  input  in_129,
  input  in_130,
  input  in_131,
  output out_132,
  output out_133,
  output out_134,
  output out_135,
  output out_136,
  output out_137,
  output out_138,
  output out_139,
  output out_140,
  output out_141,
  output out_142,
  output out_143,
  output out_144,
  output out_145,
  output out_146,
  output out_147
);

  wire mux4way16_1_out_67, mux4way16_1_out_68, mux4way16_1_out_69, mux4way16_1_out_70, mux4way16_1_out_71,
       mux4way16_1_out_72, mux4way16_1_out_73, mux4way16_1_out_74, mux4way16_1_out_75, mux4way16_1_out_76,
       mux4way16_1_out_77, mux4way16_1_out_78, mux4way16_1_out_79, mux4way16_1_out_80, mux4way16_1_out_81,
       mux4way16_1_out_82, mux4way16_2_out_67, mux4way16_2_out_68, mux4way16_2_out_69, mux4way16_2_out_70,
       mux4way16_2_out_71, mux4way16_2_out_72, mux4way16_2_out_73, mux4way16_2_out_74, mux4way16_2_out_75,
       mux4way16_2_out_76, mux4way16_2_out_77, mux4way16_2_out_78, mux4way16_2_out_79, mux4way16_2_out_80,
       mux4way16_2_out_81, mux4way16_2_out_82;

  MUX4WAY16 mux4way16_1 (
    .SEL(SEL0), .A0(in_1), .B0(in_2), .A1(in_3), .B1(in_4), .A2(in_5), .B2(in_6), .A3(in_7), .B3(in_8),
    .A4(in_9), .B4(in_10), .A5(in_11), .B5(in_12), .A6(in_13), .B6(in_14), .A7(in_15), .B7(in_16),
    .A8(in_17), .B8(in_18), .A9(in_19), .B9(in_20), .A10(in_21), .B10(in_22), .A11(in_23), .B11(in_24),
    .A12(in_25), .B12(in_26), .A13(in_27), .B13(in_28), .A14(in_29), .B14(in_30), .A15(in_31), .B15(in_32),
    .in_34(in_33), .in_35(in_34), .in_36(in_35), .in_37(in_36), .in_38(in_37), .in_39(in_38), .in_40(in_39),
    .in_41(in_40), .in_42(in_41), .in_43(in_42), .in_44(in_43), .in_45(in_44), .in_46(in_45), .in_47(in_46),
    .in_48(in_47), .in_49(in_48), .in_50(in_49), .in_51(in_50), .in_52(in_51), .in_53(in_52), .in_54(in_53),
    .in_55(in_54), .in_56(in_55), .in_57(in_56), .in_58(in_57), .in_59(in_58), .in_60(in_59), .in_61(in_61),
    .in_62(in_62), .in_63(in_63), .in_64(in_64), .in_65(in_66), .SEL1(SEL1), .out_67(mux4way16_1_out_67),
    .out_68(mux4way16_1_out_68), .out_69(mux4way16_1_out_69), .out_70(mux4way16_1_out_70),
    .out_71(mux4way16_1_out_71), .out_72(mux4way16_1_out_72), .out_73(mux4way16_1_out_73),
    .out_74(mux4way16_1_out_74), .out_75(mux4way16_1_out_75), .out_76(mux4way16_1_out_76),
    .out_77(mux4way16_1_out_77), .out_78(mux4way16_1_out_78), .out_79(mux4way16_1_out_79),
    .out_80(mux4way16_1_out_80), .out_81(mux4way16_1_out_81), .out_82(mux4way16_1_out_82));
  MUX4WAY16 mux4way16_2 (
    .SEL(SEL0), .A0(in_68), .B0(in_69), .A1(in_70), .B1(in_71), .A2(in_72), .B2(in_73), .A3(in_74),
    .B3(in_75), .A4(in_76), .B4(in_77), .A5(in_78), .B5(in_79), .A6(in_80), .B6(in_81), .A7(in_82),
    .B7(in_83), .A8(in_84), .B8(in_85), .A9(in_86), .B9(in_87), .A10(in_88), .B10(in_89), .A11(in_90),
    .B11(in_91), .A12(in_92), .B12(in_93), .A13(in_94), .B13(in_95), .A14(in_96), .B14(in_97), .A15(in_98),
    .B15(in_99), .in_34(in_100), .in_35(in_101), .in_36(in_102), .in_37(in_103), .in_38(in_104),
    .in_39(in_105), .in_40(in_106), .in_41(in_107), .in_42(in_108), .in_43(in_109), .in_44(in_110),
    .in_45(in_111), .in_46(in_112), .in_47(in_113), .in_48(in_114), .in_49(in_115), .in_50(in_116),
    .in_51(in_117), .in_52(in_118), .in_53(in_119), .in_54(in_120), .in_55(in_121), .in_56(in_122),
    .in_57(in_123), .in_58(in_124), .in_59(in_125), .in_60(in_126), .in_61(in_127), .in_62(in_128),
    .in_63(in_129), .in_64(in_130), .in_65(in_131), .SEL1(SEL1), .out_67(mux4way16_2_out_67),
    .out_68(mux4way16_2_out_68), .out_69(mux4way16_2_out_69), .out_70(mux4way16_2_out_70),
    .out_71(mux4way16_2_out_71), .out_72(mux4way16_2_out_72), .out_73(mux4way16_2_out_73),
    .out_74(mux4way16_2_out_74), .out_75(mux4way16_2_out_75), .out_76(mux4way16_2_out_76),
    .out_77(mux4way16_2_out_77), .out_78(mux4way16_2_out_78), .out_79(mux4way16_2_out_79),
    .out_80(mux4way16_2_out_80), .out_81(mux4way16_2_out_81), .out_82(mux4way16_2_out_82));
  MUX16 mux16_1 (
    .SEL(SEL2), .A0(mux4way16_1_out_67), .B0(mux4way16_2_out_67), .A1(mux4way16_1_out_68),
    .B1(mux4way16_2_out_68), .A2(mux4way16_1_out_69), .B2(mux4way16_2_out_69), .A3(mux4way16_1_out_70),
    .B3(mux4way16_2_out_70), .A4(mux4way16_1_out_71), .B4(mux4way16_2_out_71), .A5(mux4way16_1_out_72),
    .B5(mux4way16_2_out_72), .A6(mux4way16_1_out_73), .B6(mux4way16_2_out_73), .A7(mux4way16_1_out_74),
    .B7(mux4way16_2_out_74), .A8(mux4way16_1_out_75), .B8(mux4way16_2_out_75), .A9(mux4way16_1_out_76),
    .B9(mux4way16_2_out_76), .A10(mux4way16_1_out_77), .B10(mux4way16_2_out_77), .A11(mux4way16_1_out_78),
    .B11(mux4way16_2_out_78), .A12(mux4way16_1_out_79), .B12(mux4way16_2_out_79), .A13(mux4way16_1_out_80),
    .B13(mux4way16_2_out_80), .A14(mux4way16_1_out_81), .B14(mux4way16_2_out_81), .A15(mux4way16_1_out_82),
    .B15(mux4way16_2_out_82), .out_34(out_132), .out_35(out_133), .out_36(out_134), .out_37(out_135),
    .out_38(out_136), .out_39(out_137), .out_40(out_138), .out_41(out_139), .out_42(out_140),
    .out_43(out_141), .out_44(out_142), .out_45(out_143), .out_46(out_144), .out_47(out_145),
    .out_48(out_146), .out_49(out_147));
endmodule

module DMUX4WAY (
  input  IN,
  input  SEL0,
  input  SEL1,
  output out_4,
  output out_5,
  output out_6,
  output out_7
);

  wire dmux2t_1_a, dmux2t_1_b;

  DMUX2T dmux2t_1 (.IN(IN), .SEL(SEL1), .A(dmux2t_1_a), .B(dmux2t_1_b));
  DMUX2T dmux2t_2 (.IN(dmux2t_1_a), .SEL(SEL0), .A(out_4), .B(out_5));
  DMUX2T dmux2t_3 (.IN(dmux2t_1_b), .SEL(SEL0), .A(out_6), .B(out_7));
  OR8WAY or8way_1 ();  // open: in_1, in_2, in_3, in_4, in_5, in_6, in_7, in_8, out_9
endmodule

module DMUX8WAY (
  input  IN,
  input  SEL1,
  input  SEL2,
  input  SEL3,
  output out_5,
  output out_6,
  output out_7,
  output out_8,
  output out_9,
  output out_10,
  output out_11,
  output out_12
);

  wire dmux2t_1_a, dmux2t_1_b;

  DMUX2T dmux2t_1 (.IN(IN), .SEL(SEL3), .A(dmux2t_1_a), .B(dmux2t_1_b));
  DMUX4WAY dmux4way_1 (
    .IN(dmux2t_1_a), .SEL0(SEL1), .SEL1(SEL2), .out_4(out_5), .out_5(out_6), .out_6(out_7), .out_7(out_8));
  DMUX4WAY dmux4way_2 (
    .IN(dmux2t_1_b), .SEL0(SEL1), .SEL1(SEL2), .out_4(out_9), .out_5(out_10), .out_6(out_11), .out_7(out_12));
endmodule
