// Logisim project Proyecto02.circ as structural Verilog: 5 circuits, main circuit HalfAdder
module HalfAdder (
  input  A,
  input  B,
  output SUM,
  output CARRY
);

  xor xor_1 (SUM, A, B);
  and and_1 (CARRY, A, B);
endmodule

module FullAdder (
  input  A,
  input  B,
  input  C,
  output CARRY,
  output SUM
);

  wire halfadder_1_carry, halfadder_1_sum, halfadder_2_carry;

  HalfAdder halfadder_1 (.A(A), .B(B), .SUM(halfadder_1_sum), .CARRY(halfadder_1_carry));
  HalfAdder halfadder_2 (.A(C), .B(halfadder_1_sum), .SUM(SUM), .CARRY(halfadder_2_carry));
  or or_1 (CARRY, halfadder_1_carry, halfadder_2_carry);
endmodule

module Add16 (
  input  [15:0] in_1,
  input  [15:0] in_2,
  output [15:0] out_3
);

  wire fulladder_1_carry, fulladder_2_carry, fulladder_3_carry, fulladder_4_carry, fulladder_5_carry,
       fulladder_6_carry, fulladder_7_carry, fulladder_8_carry, fulladder_9_carry, fulladder_10_carry,
       fulladder_11_carry, fulladder_12_carry, fulladder_13_carry, fulladder_14_carry, halfadder_1_carry;

  HalfAdder halfadder_1 (.A(in_1[0]), .B(in_2[0]), .SUM(out_3[0]), .CARRY(halfadder_1_carry));
  FullAdder fulladder_1 (.A(in_1[1]), .B(in_2[1]), .C(halfadder_1_carry), .CARRY(fulladder_1_carry), .SUM(out_3[1]));
  FullAdder fulladder_2 (.A(in_1[2]), .B(in_2[2]), .C(fulladder_1_carry), .CARRY(fulladder_2_carry), .SUM(out_3[2]));
  FullAdder fulladder_3 (.A(in_1[3]), .B(in_2[3]), .C(fulladder_2_carry), .CARRY(fulladder_3_carry), .SUM(out_3[3]));
  FullAdder fulladder_4 (.A(in_1[4]), .B(in_2[4]), .C(fulladder_3_carry), .CARRY(fulladder_4_carry), .SUM(out_3[4]));
  FullAdder fulladder_5 (.A(in_1[5]), .B(in_2[5]), .C(fulladder_4_carry), .CARRY(fulladder_5_carry), .SUM(out_3[5]));
  FullAdder fulladder_6 (.A(in_1[6]), .B(in_2[6]), .C(fulladder_5_carry), .CARRY(fulladder_6_carry), .SUM(out_3[6]));
  FullAdder fulladder_7 (.A(in_1[7]), .B(in_2[7]), .C(fulladder_6_carry), .CARRY(fulladder_7_carry), .SUM(out_3[7]));
  FullAdder fulladder_8 (.A(in_1[8]), .B(in_2[8]), .C(fulladder_7_carry), .CARRY(fulladder_8_carry), .SUM(out_3[8]));
  FullAdder fulladder_9 (.A(in_1[9]), .B(in_2[9]), .C(fulladder_8_carry), .CARRY(fulladder_9_carry), .SUM(out_3[9]));
  FullAdder fulladder_10 (
    .A(in_1[10]), .B(in_2[10]), .C(fulladder_9_carry), .CARRY(fulladder_10_carry), .SUM(out_3[10]));
  FullAdder fulladder_11 (
    .A(in_1[11]), .B(in_2[11]), .C(fulladder_10_carry), .CARRY(fulladder_11_carry), .SUM(out_3[11]));
  FullAdder fulladder_12 (
    .A(in_1[12]), .B(in_2[12]), .C(fulladder_11_carry), .CARRY(fulladder_12_carry), .SUM(out_3[12]));
  FullAdder fulladder_13 (
    .A(in_1[13]), .B(in_2[13]), .C(fulladder_12_carry), .CARRY(fulladder_13_carry), .SUM(out_3[13]));
  FullAdder fulladder_14 (
    .A(in_1[14]), .B(in_2[14]), .C(fulladder_13_carry), .CARRY(fulladder_14_carry), .SUM(out_3[14]));
  FullAdder fulladder_15 (.A(in_1[15]), .B(in_2[15]), .C(fulladder_14_carry), .SUM(out_3[15]));  // open: CARRY
endmodule

module Inc16 (
  input  [15:0] A,
  output [15:0] out_2
);

  Add16 add16_1 (.in_1(A), .in_2(16'h1), .out_3(out_2));
endmodule

module ALU (
  input  [15:0] X,
  input  ZX,
  input  NX,
  input  [15:0] Y,
  input  ZY,
  input  NY,
  input  F,
  input  NO,
  output ZR,
  output NG,
  output [15:0] OUT
);

  wire or_1_out, or_2_out, or_3_out;
  wire [15:0] add16_1_out_3, and_1_out, multiplexer_1_out, multiplexer_2_out, multiplexer_3_out,
       multiplexer_4_out, multiplexer_5_out, not_1_out, not_2_out, not_3_out;

  Multiplexer #(.width(16), .enable("false")) multiplexer_1 (
    .in0(X), .in1({16{1'b0}}), .out(multiplexer_1_out), .sel(ZX));
  Multiplexer #(.width(16), .enable("false")) multiplexer_2 (
    .in0(Y), .in1({16{1'b0}}), .out(multiplexer_2_out), .sel(ZY));
  assign not_1_out = ~multiplexer_1_out;  // NOT_Gate not_1, 16 bits wide
  assign not_2_out = ~multiplexer_2_out;  // NOT_Gate not_2, 16 bits wide
  Multiplexer #(.width(16), .enable("false")) multiplexer_3 (
    .in0(multiplexer_1_out), .in1(not_1_out), .out(multiplexer_3_out), .sel(NX));
  Multiplexer #(.width(16), .enable("false")) multiplexer_4 (
    .in0(multiplexer_2_out), .in1(not_2_out), .out(multiplexer_4_out), .sel(NY));
  Add16 add16_1 (.in_1(multiplexer_3_out), .in_2(multiplexer_4_out), .out_3(add16_1_out_3));
  assign and_1_out = multiplexer_3_out & multiplexer_4_out;  // AND_Gate and_1, 16 bits wide
  Multiplexer #(.width(16), .enable("false")) multiplexer_5 (
    .in0(and_1_out), .in1(add16_1_out_3), .out(multiplexer_5_out), .sel(F));
  assign not_3_out = ~multiplexer_5_out;  // NOT_Gate not_3, 16 bits wide
  Multiplexer #(.width(16), .enable("false")) multiplexer_6 (
    .in0(multiplexer_5_out), .in1(not_3_out), .out({NG, OUT[14:0]}), .sel(NO));
  or or_1 (or_1_out, OUT[0], OUT[1], OUT[2], OUT[3], OUT[4], OUT[5], OUT[6], OUT[7]);
  or or_2 (or_2_out, OUT[8], OUT[9], OUT[10], OUT[11], OUT[12], OUT[13], OUT[14], NG);
  or or_3 (or_3_out, or_1_out, or_2_out);
  not not_4 (ZR, or_3_out);

  assign OUT[15] = NG;
endmodule
