// Logisim project Proyecto03.circ as structural Verilog
module BIT (
  input  IN,
  input  LOAD,
  input  CLK,
  output OUT
);

  wire multiplexer_1_out;

  Multiplexer #(.enable("false")) multiplexer_1 (.in0(OUT), .in1(IN), .out(multiplexer_1_out), .sel(LOAD));
  D_Flip_Flop d_ff_1 (.clk(CLK), .D(multiplexer_1_out), .Q(OUT));  // open: Qn, preset, en, reset
endmodule

module REGISTER (
  input  [15:0] IN,
  input  LOAD,
  input  CLK,
  output [15:0] OUT
);

  BIT bit_1 (.IN(IN[0]), .LOAD(LOAD), .CLK(CLK), .OUT(OUT[0]));
  BIT bit_2 (.IN(IN[1]), .LOAD(LOAD), .CLK(CLK), .OUT(OUT[1]));
  BIT bit_3 (.IN(IN[2]), .LOAD(LOAD), .CLK(CLK), .OUT(OUT[2]));
  BIT bit_4 (.IN(IN[3]), .LOAD(LOAD), .CLK(CLK), .OUT(OUT[3]));
  BIT bit_5 (.IN(IN[4]), .LOAD(LOAD), .CLK(CLK), .OUT(OUT[4]));
  BIT bit_6 (.IN(IN[5]), .LOAD(LOAD), .CLK(CLK), .OUT(OUT[5]));
  BIT bit_7 (.IN(IN[6]), .LOAD(LOAD), .CLK(CLK), .OUT(OUT[6]));
  BIT bit_8 (.IN(IN[7]), .LOAD(LOAD), .CLK(CLK), .OUT(OUT[7]));
  BIT bit_9 (.IN(IN[8]), .LOAD(LOAD), .CLK(CLK), .OUT(OUT[8]));
  BIT bit_10 (.IN(IN[9]), .LOAD(LOAD), .CLK(CLK), .OUT(OUT[9]));
  BIT bit_11 (.IN(IN[10]), .LOAD(LOAD), .CLK(CLK), .OUT(OUT[10]));
  BIT bit_12 (.IN(IN[11]), .LOAD(LOAD), .CLK(CLK), .OUT(OUT[11]));
  BIT bit_13 (.IN(IN[12]), .LOAD(LOAD), .CLK(CLK), .OUT(OUT[12]));
  BIT bit_14 (.IN(IN[13]), .LOAD(LOAD), .CLK(CLK), .OUT(OUT[13]));
  BIT bit_15 (.IN(IN[14]), .LOAD(LOAD), .CLK(CLK), .OUT(OUT[14]));
  BIT bit_16 (.IN(IN[15]), .LOAD(LOAD), .CLK(CLK), .OUT(OUT[15]));
endmodule

module RAM8 (
  input  [15:0] IN,
  input  LOAD,
  input  [2:0] ADDRESS,
  input  CLK,
  output [15:0] out_5
);

  wire demultiplexer_1_out0;
  wire [15:0] register_1_out, register_2_out, register_3_out, register_4_out, register_5_out, register_6_out,
       register_7_out, register_8_out;

  Demultiplexer #(.select(3), .enable("false")) demultiplexer_1 (
    .out0(demultiplexer_1_out0), .in(LOAD), .sel(ADDRESS));  // open: out1, out2, out3, out4, out5, out6, out7
  REGISTER register_1 (.IN(IN), .LOAD(demultiplexer_1_out0), .CLK(CLK), .OUT(register_1_out));
  REGISTER register_2 (.IN(IN), .LOAD(demultiplexer_1_out0), .CLK(CLK), .OUT(register_2_out));
  REGISTER register_3 (.IN(IN), .LOAD(demultiplexer_1_out0), .CLK(CLK), .OUT(register_3_out));
  REGISTER register_4 (.IN(IN), .LOAD(demultiplexer_1_out0), .CLK(CLK), .OUT(register_4_out));
  REGISTER register_5 (.IN(IN), .LOAD(demultiplexer_1_out0), .CLK(CLK), .OUT(register_5_out));
  REGISTER register_6 (.IN(IN), .LOAD(demultiplexer_1_out0), .CLK(CLK), .OUT(register_6_out));
  REGISTER register_7 (.IN(IN), .LOAD(demultiplexer_1_out0), .CLK(CLK), .OUT(register_7_out));
  REGISTER register_8 (.IN(IN), .LOAD(demultiplexer_1_out0), .CLK(CLK), .OUT(register_8_out));
  Multiplexer #(.select(3), .width(16), .enable("false")) multiplexer_1 (
    .in0(register_1_out), .in1(register_2_out), .in2(register_3_out), .in3(register_4_out),
    .in4(register_5_out), .in5(register_6_out), .in6(register_7_out), .in7(register_8_out), .out(out_5),
    .sel(ADDRESS));
endmodule

module RAM64 (
  input  [15:0] IN,
  input  LOAD,
  input  [5:0] ADDRESS,
  input  CLK,
  output [15:0] OUT
);

  wire demultiplexer_1_out0, demultiplexer_1_out1, demultiplexer_1_out2, demultiplexer_1_out3,
       demultiplexer_1_out4, demultiplexer_1_out5, demultiplexer_1_out6, demultiplexer_1_out7;
  wire [15:0] ram8_1_out_5, ram8_2_out_5, ram8_3_out_5, ram8_4_out_5, ram8_5_out_5, ram8_6_out_5,
       ram8_7_out_5, ram8_8_out_5;

  Demultiplexer #(.select(3), .enable("false")) demultiplexer_1 (
    .out0(demultiplexer_1_out0), .out1(demultiplexer_1_out1), .out2(demultiplexer_1_out2),
    .out3(demultiplexer_1_out3), .out4(demultiplexer_1_out4), .out5(demultiplexer_1_out5),
    .out6(demultiplexer_1_out6), .out7(demultiplexer_1_out7), .in(LOAD), .sel(ADDRESS[5:3]));
  RAM8 ram8_1 (.IN(IN), .LOAD(demultiplexer_1_out0), .ADDRESS(ADDRESS[2:0]), .CLK(CLK), .out_5(ram8_1_out_5));
  RAM8 ram8_2 (.IN(IN), .LOAD(demultiplexer_1_out1), .ADDRESS(ADDRESS[2:0]), .CLK(CLK), .out_5(ram8_2_out_5));
  RAM8 ram8_3 (.IN(IN), .LOAD(demultiplexer_1_out2), .ADDRESS(ADDRESS[2:0]), .CLK(CLK), .out_5(ram8_3_out_5));
  RAM8 ram8_4 (.IN(IN), .LOAD(demultiplexer_1_out3), .ADDRESS(ADDRESS[2:0]), .CLK(CLK), .out_5(ram8_4_out_5));
  RAM8 ram8_5 (.IN(IN), .LOAD(demultiplexer_1_out4), .ADDRESS(ADDRESS[2:0]), .CLK(CLK), .out_5(ram8_5_out_5));
  RAM8 ram8_6 (.IN(IN), .LOAD(demultiplexer_1_out5), .ADDRESS(ADDRESS[2:0]), .CLK(CLK), .out_5(ram8_6_out_5));
  RAM8 ram8_7 (.IN(IN), .LOAD(demultiplexer_1_out6), .ADDRESS(ADDRESS[2:0]), .CLK(CLK), .out_5(ram8_7_out_5));
  RAM8 ram8_8 (.IN(IN), .LOAD(demultiplexer_1_out7), .ADDRESS(ADDRESS[2:0]), .CLK(CLK), .out_5(ram8_8_out_5));
  Multiplexer #(.select(3), .width(16), .enable("false")) multiplexer_1 (
    .in0(ram8_1_out_5), .in1(ram8_2_out_5), .in2(ram8_3_out_5), .in3(ram8_4_out_5), .in4(ram8_5_out_5),
    .in5(ram8_6_out_5), .in6(ram8_7_out_5), .in7(ram8_8_out_5), .out(OUT), .sel(ADDRESS[5:3]));
endmodule

module RAM512 (
  input  [15:0] IN,
  input  LOAD,
  input  [8:0] in_3,
  input  CLK,
  output [15:0] out_5
);

  wire demultiplexer_1_out0, demultiplexer_1_out1, demultiplexer_1_out2, demultiplexer_1_out4,
       demultiplexer_1_out5, demultiplexer_1_out6, demultiplexer_1_out7;
  wire [15:0] ram64_1_out, ram64_2_out, ram64_3_out, ram64_4_out, ram64_5_out, ram64_6_out, ram64_7_out,
       ram64_8_out;

  Demultiplexer #(.select(3), .enable("false")) demultiplexer_1 (
    .out0(demultiplexer_1_out0), .out1(demultiplexer_1_out1), .out2(demultiplexer_1_out2), .out3(CLK),
    .out4(demultiplexer_1_out4), .out5(demultiplexer_1_out5), .out6(demultiplexer_1_out6),
    .out7(demultiplexer_1_out7), .in(LOAD), .sel(in_3[8:6]));
  RAM64 ram64_1 (.IN(IN), .LOAD(demultiplexer_1_out0), .ADDRESS(in_3[5:0]), .CLK(CLK), .OUT(ram64_1_out));
  RAM64 ram64_2 (.IN(IN), .LOAD(demultiplexer_1_out1), .ADDRESS(in_3[5:0]), .CLK(CLK), .OUT(ram64_2_out));
  RAM64 ram64_3 (.IN(IN), .LOAD(demultiplexer_1_out2), .ADDRESS(in_3[5:0]), .CLK(CLK), .OUT(ram64_3_out));
  RAM64 ram64_4 (.IN(IN), .LOAD(CLK), .ADDRESS(in_3[5:0]), .CLK(CLK), .OUT(ram64_4_out));
  RAM64 ram64_5 (.IN(IN), .LOAD(demultiplexer_1_out4), .ADDRESS(in_3[5:0]), .CLK(CLK), .OUT(ram64_5_out));
  RAM64 ram64_6 (.IN(IN), .LOAD(demultiplexer_1_out5), .ADDRESS(in_3[5:0]), .CLK(CLK), .OUT(ram64_6_out));
  RAM64 ram64_7 (.IN(IN), .LOAD(demultiplexer_1_out6), .ADDRESS(in_3[5:0]), .CLK(CLK), .OUT(ram64_7_out));
  RAM64 ram64_8 (.IN(IN), .LOAD(demultiplexer_1_out7), .ADDRESS(in_3[5:0]), .CLK(CLK), .OUT(ram64_8_out));
  Multiplexer #(.select(3), .width(16), .enable("false")) multiplexer_1 (
    .in0(ram64_1_out), .in1(ram64_2_out), .in2(ram64_3_out), .in3(ram64_4_out), .in4(ram64_5_out),
    .in5(ram64_6_out), .in6(ram64_7_out), .in7(ram64_8_out), .out(out_5), .sel(in_3[8:6]));
endmodule

module PC (
  input  [15:0] IN,
  input  LOAD,
  input  INC,
  input  RESET,
  input  CLK,
  output [15:0] out_6
);

  wire [15:0] inc16_1_out_2, multiplexer_1_out, multiplexer_2_out, multiplexer_3_out;

  INC16 inc16_1 (.in_1(out_6), .out_2(inc16_1_out_2));
  Multiplexer #(.width(16), .enable("false")) multiplexer_1 (
    .in0(out_6), .in1(inc16_1_out_2), .out(multiplexer_1_out), .sel(INC));
  Multiplexer #(.width(16), .enable("false")) multiplexer_2 (
    .in0(multiplexer_1_out), .in1(IN), .out(multiplexer_2_out), .sel(LOAD));
  Multiplexer #(.width(16), .enable("false")) multiplexer_3 (
    .in0(multiplexer_2_out), .in1({16{1'b0}}), .out(multiplexer_3_out), .sel(RESET));
  REGISTER register_1 (.IN(multiplexer_3_out), .LOAD(1'b1), .CLK(CLK), .OUT(out_6));
endmodule

module INC16 (
  input  [15:0] in_1,
  output [15:0] out_2
);

  Adder #(.width(16)) adder_1 (.a(in_1), .b(16'h1), .out(out_2));  // open: cin, cout
endmodule
