// Logisim project Proyecto05.circ as structural Verilog: 3 circuits, main circuit CPU
module CPU (
  input  [15:0] IN_M,
  input  [15:0] Instruccion,
  input  reset,
  input  clear,
  output [15:0] outM,
  output [14:0] ADDRESS,
  output [15:0] outPC,
  output writeM
);

  wire alu_1_ng, alu_1_zr, and_3_out, and_4_out, and_5_out, and_6_out, CLK, inA, inD, not_1_out, not_2_out,
       not_3_out, or_2_out, or_3_out;
  wire [15:0] D_q, multiplexer_1_out, multiplexer_2_out;
  wire [15:15] A_q;

  Clock clock_1 (.out(CLK));
  and and_1 (inD, Instruccion[4], Instruccion[15]);
  and and_2 (writeM, Instruccion[3], Instruccion[15]);
  not not_1 (not_1_out, Instruccion[15]);
  not not_2 (not_2_out, Instruccion[15]);
  or or_1 (inA, Instruccion[5], not_1_out);
  Multiplexer #(.width(16), .enable("false")) multiplexer_1 (
    .in0(outM), .in1(Instruccion), .out(multiplexer_1_out), .sel(not_2_out));
  Register #(.width(16)) A (.D(multiplexer_1_out), .en(inA), .Q({A_q[15], ADDRESS}), .clk(CLK), .clr(clear));
  Register #(.width(16)) D (.D(outM), .en(inD), .Q(D_q), .clk(CLK), .clr(clear));
  Multiplexer #(.width(16), .enable("false")) multiplexer_2 (
    .in0({A_q[15], ADDRESS}), .in1(IN_M), .out(multiplexer_2_out), .sel(Instruccion[12]));
  ALU alu_1 (
    .X(D_q), .ZX(Instruccion[11]), .NX(Instruccion[10]), .Y(multiplexer_2_out), .ZY(Instruccion[9]),
    .NY(Instruccion[8]), .F(Instruccion[7]), .NO(Instruccion[6]), .ZR(alu_1_zr), .NG(alu_1_ng), .OUT(outM));
  or or_2 (or_2_out, alu_1_zr, alu_1_ng);
  not not_3 (not_3_out, or_2_out);
  PC PC (.IN({A_q[15], ADDRESS}), .LOAD(and_6_out), .INC(1'b1), .RESET(reset), .CLK(CLK), .out_6(outPC));
  and and_3 (and_3_out, alu_1_ng, Instruccion[2]);
  and and_4 (and_4_out, alu_1_zr, Instruccion[1]);
  and and_5 (and_5_out, not_3_out, Instruccion[0]);
  or or_3 (or_3_out, and_3_out, and_4_out, and_5_out);
  and and_6 (and_6_out, Instruccion[15], or_3_out);

  // Other names for the same wires on the sheet: clr = clear; J3 = Instruccion[0]; J2 = Instruccion[1];
  //   J1 = Instruccion[2]; d3 = Instruccion[3]; d2 = Instruccion[4]; d1 = Instruccion[5]; c6 = Instruccion[6];
  //   c5 = Instruccion[7]; c4 = Instruccion[8]; c3 = Instruccion[9]; c2 = Instruccion[10]; c1 = Instruccion[11];
  //   a = Instruccion[12]; C_A = Instruccion[15]
endmodule

module COMPUTER (
  input  RESET,
  input  clear,
  input  str
);

  wire clock_1_out, cpu_1_writem;
  wire [14:0] cpu_1_address;
  wire [15:0] cpu_1_outm, cpu_1_outpc, memory_1_out_7, rom_1_data;

  ROM #(.addrWidth(16), .dataWidth(16)) rom_1 (.addr(cpu_1_outpc), .data(rom_1_data));  // open: sel
  CPU cpu_1 (
    .IN_M(memory_1_out_7), .Instruccion(rom_1_data), .reset(RESET), .clear(clear), .outM(cpu_1_outm),
    .ADDRESS(cpu_1_address), .outPC(cpu_1_outpc), .writeM(cpu_1_writem));
  Clock clock_1 (.out(clock_1_out));
  MEMORY memory_1 (
    .address(cpu_1_address), .in(cpu_1_outm), .load(cpu_1_writem), .str(str), .clr(clear), .CLK(clock_1_out),
    .out_7(memory_1_out_7));
endmodule

module MEMORY (
  input  [14:0] address,
  input  [15:0] in,
  input  load,
  input  str,
  input  clr,
  input  CLK,
  output [15:0] out_7
);

  RAM #(.addrWidth(14), .dataWidth(16), .bus("separate")) ram_1 (
    .addr(address[13:0]), .din(in), .data(out_7), .str(str), .sel(1'b1), .clk(CLK), .ld(load), .clr(clr));
endmodule
